// Logisim project FULL ALU.circ as structural Verilog: 10 circuits, main circuit main
module main (
  input  [15:0] A,
  input  [15:0] B,
  input  [5:0] in_3,
  output [15:0] ALU_RESULT,
  output ZERO_FLAG,
  output GREAT_FLAG,
  output LESS_FLAG,
  output OVER_FLOW
);

  wire R0, R1, R2, SUB;
  wire [15:0] RES0, RES1, RES2, SLT, SLTE, SLTEU, SLTU;

  ALU_CONTROL alu_control_1 (
    .S5(in_3[5]), .S4(in_3[4]), .S3(in_3[3]), .S2(in_3[2]), .S1(in_3[1]), .S0(in_3[0]), .A(R2), .B(R1), .C(R0));
  or or_1 (SUB, R0, R2);
  SHIFIT_UNIT shifit_unit_1 (.shift_rotate_amount(B[3:0]), .A(A), .result(RES1), .selector(in_3[1:0]));
  LOGIC_UNIT logic_unit_1 (.A(A), .B(B), .LOGIC_RESULT(RES0), .SELECTOR(in_3[1:0]));
  ARITHMATIC_UNIT arithmatic_unit_1 (
    .sub(SUB), .A(A), .B(B), .RESULT(RES2), .Zero_flag(ZERO_FLAG), .SLTEU(SLTEU), .SLTU(SLTU),
    .GREAT_FLAG(GREAT_FLAG), .SLTE(SLTE), .LESS_FLAG(LESS_FLAG), .SLT(SLT), .overflow(OVER_FLOW));
  Multiplexer #(.select(3), .width(16)) multiplexer_1 (
    .in0(RES0), .in1(RES1), .in2(RES2), .in3(RES2), .in4(SLT), .in5(SLTU), .in6(SLTE), .in7(SLTEU),
    .out(ALU_RESULT), .sel(in_3[4:2]));  // open: en

  // Other names for the same wires on the sheet: S0 = in_3[0]; S1 = in_3[1]; S2 = in_3[2]; S3 = in_3[3]; S4 = in_3[4];
  //   S5 = in_3[5]; SHIFT_ROTAT[3:0] = B[3:0]
endmodule

// 16_BITS AND
module AND_GATES (
  input  [15:0] A,
  input  [15:0] B,
  output [15:0] AND_RESULT
);

  and and_1 (AND_RESULT[0], A[0], B[0]);
  and and_2 (AND_RESULT[1], A[1], B[1]);
  and and_3 (AND_RESULT[2], A[2], B[2]);
  and and_4 (AND_RESULT[3], A[3], B[3]);
  and and_5 (AND_RESULT[4], A[4], B[4]);
  and and_6 (AND_RESULT[5], A[5], B[5]);
  and and_7 (AND_RESULT[6], A[6], B[6]);
  and and_8 (AND_RESULT[7], A[7], B[7]);
  and and_9 (AND_RESULT[8], A[8], B[8]);
  and and_10 (AND_RESULT[9], A[9], B[9]);
  and and_11 (AND_RESULT[10], A[10], B[10]);
  and and_12 (AND_RESULT[11], A[11], B[11]);
  and and_13 (AND_RESULT[12], A[12], B[12]);
  and and_14 (AND_RESULT[13], A[13], B[13]);
  and and_15 (AND_RESULT[14], A[14], B[14]);
  and and_16 (AND_RESULT[15], A[15], B[15]);
endmodule

// 16_BITS OR
module OR_GATES (
  input  [15:0] A,
  input  [15:0] B,
  output [15:0] OR_RESULT
);

  or or_1 (OR_RESULT[0], A[0], B[0]);
  or or_2 (OR_RESULT[1], A[1], B[1]);
  or or_3 (OR_RESULT[2], A[2], B[2]);
  or or_4 (OR_RESULT[3], A[3], B[3]);
  or or_5 (OR_RESULT[4], A[4], B[4]);
  or or_6 (OR_RESULT[5], A[5], B[5]);
  or or_7 (OR_RESULT[6], A[6], B[6]);
  or or_8 (OR_RESULT[7], A[7], B[7]);
  or or_9 (OR_RESULT[8], A[8], B[8]);
  or or_10 (OR_RESULT[9], A[9], B[9]);
  or or_11 (OR_RESULT[10], A[10], B[10]);
  or or_12 (OR_RESULT[11], A[11], B[11]);
  or or_13 (OR_RESULT[12], A[12], B[12]);
  or or_14 (OR_RESULT[13], A[13], B[13]);
  or or_15 (OR_RESULT[14], A[14], B[14]);
  or or_16 (OR_RESULT[15], A[15], B[15]);
endmodule

// 16_BITS XOR
module XOR_GATES (
  input  [15:0] A,
  input  [15:0] B,
  output [15:0] XOR_RESULT
);

  xor xor_1 (XOR_RESULT[0], A[0], B[0]);
  xor xor_2 (XOR_RESULT[1], A[1], B[1]);
  xor xor_3 (XOR_RESULT[2], A[2], B[2]);
  xor xor_4 (XOR_RESULT[3], A[3], B[3]);
  xor xor_5 (XOR_RESULT[4], A[4], B[4]);
  xor xor_6 (XOR_RESULT[5], A[5], B[5]);
  xor xor_7 (XOR_RESULT[6], A[6], B[6]);
  xor xor_8 (XOR_RESULT[7], A[7], B[7]);
  xor xor_9 (XOR_RESULT[8], A[8], B[8]);
  xor xor_10 (XOR_RESULT[9], A[9], B[9]);
  xor xor_11 (XOR_RESULT[10], A[10], B[10]);
  xor xor_12 (XOR_RESULT[11], A[11], B[11]);
  xor xor_13 (XOR_RESULT[12], A[12], B[12]);
  xor xor_14 (XOR_RESULT[13], A[13], B[13]);
  xor xor_15 (XOR_RESULT[14], A[14], B[14]);
  xor xor_16 (XOR_RESULT[15], A[15], B[15]);
endmodule

// 16_BITS NOR
module NOR_GATES (
  input  [15:0] A,
  input  [15:0] B,
  output [15:0] NOR_RESULT
);

  nor nor_1 (NOR_RESULT[0], A[0], B[0]);
  nor nor_2 (NOR_RESULT[1], A[1], B[1]);
  nor nor_3 (NOR_RESULT[2], A[2], B[2]);
  nor nor_4 (NOR_RESULT[3], A[3], B[3]);
  nor nor_5 (NOR_RESULT[4], A[4], B[4]);
  nor nor_6 (NOR_RESULT[5], A[5], B[5]);
  nor nor_7 (NOR_RESULT[6], A[6], B[6]);
  nor nor_8 (NOR_RESULT[7], A[7], B[7]);
  nor nor_9 (NOR_RESULT[8], A[8], B[8]);
  nor nor_10 (NOR_RESULT[9], A[9], B[9]);
  nor nor_11 (NOR_RESULT[10], A[10], B[10]);
  nor nor_12 (NOR_RESULT[11], A[11], B[11]);
  nor nor_13 (NOR_RESULT[12], A[12], B[12]);
  nor nor_14 (NOR_RESULT[13], A[13], B[13]);
  nor nor_15 (NOR_RESULT[14], A[14], B[14]);
  nor nor_16 (NOR_RESULT[15], A[15], B[15]);
endmodule

module ADD_SUB (
  input  A,
  input  B,
  input  SUB,
  input  CARRY_IN,
  output result,
  output Cout
);

  wire xor_1_out;

  xor xor_1 (xor_1_out, SUB, B);
  Adder #(.width(1)) adder_1 (.a(A), .b(xor_1_out), .out(result), .cin(CARRY_IN), .cout(Cout));

  // Other names for the same wires on the sheet: Cin = CARRY_IN
endmodule

module ARITHMATIC_UNIT (
  input  sub,
  input  [15:0] A,
  input  [15:0] B,
  output [15:0] RESULT,
  output Zero_flag,
  output [15:0] SLTEU,
  output [15:0] SLTU,
  output GREAT_FLAG,
  output [15:0] SLTE,
  output LESS_FLAG,
  output [15:0] SLT,
  output overflow
);

  wire add_sub_1_cout, add_sub_2_cout, add_sub_3_cout, add_sub_4_cout, add_sub_5_cout, add_sub_6_cout,
       add_sub_7_cout, add_sub_8_cout, add_sub_9_cout, add_sub_10_cout, add_sub_11_cout, add_sub_12_cout,
       add_sub_13_cout, add_sub_14_cout, add_sub_15_cout, and_1_out, nand_1_out, or_3_out, OVER;

  ADD_SUB add_sub_1 (.A(A[0]), .B(B[0]), .SUB(sub), .CARRY_IN(sub), .result(RESULT[0]), .Cout(add_sub_1_cout));
  ADD_SUB add_sub_2 (
    .A(A[1]), .B(B[1]), .SUB(sub), .CARRY_IN(add_sub_1_cout), .result(RESULT[1]), .Cout(add_sub_2_cout));
  ADD_SUB add_sub_3 (
    .A(A[2]), .B(B[2]), .SUB(sub), .CARRY_IN(add_sub_2_cout), .result(RESULT[2]), .Cout(add_sub_3_cout));
  ADD_SUB add_sub_4 (
    .A(A[3]), .B(B[3]), .SUB(sub), .CARRY_IN(add_sub_3_cout), .result(RESULT[3]), .Cout(add_sub_4_cout));
  ADD_SUB add_sub_5 (
    .A(A[4]), .B(B[4]), .SUB(sub), .CARRY_IN(add_sub_4_cout), .result(RESULT[4]), .Cout(add_sub_5_cout));
  ADD_SUB add_sub_6 (
    .A(A[5]), .B(B[5]), .SUB(sub), .CARRY_IN(add_sub_5_cout), .result(RESULT[5]), .Cout(add_sub_6_cout));
  ADD_SUB add_sub_7 (
    .A(A[6]), .B(B[6]), .SUB(sub), .CARRY_IN(add_sub_6_cout), .result(RESULT[6]), .Cout(add_sub_7_cout));
  ADD_SUB add_sub_8 (
    .A(A[7]), .B(B[7]), .SUB(sub), .CARRY_IN(add_sub_7_cout), .result(RESULT[7]), .Cout(add_sub_8_cout));
  ADD_SUB add_sub_9 (
    .A(A[8]), .B(B[8]), .SUB(sub), .CARRY_IN(add_sub_8_cout), .result(RESULT[8]), .Cout(add_sub_9_cout));
  ADD_SUB add_sub_10 (
    .A(A[9]), .B(B[9]), .SUB(sub), .CARRY_IN(add_sub_9_cout), .result(RESULT[9]), .Cout(add_sub_10_cout));
  ADD_SUB add_sub_11 (
    .A(A[10]), .B(B[10]), .SUB(sub), .CARRY_IN(add_sub_10_cout), .result(RESULT[10]), .Cout(add_sub_11_cout));
  ADD_SUB add_sub_12 (
    .A(A[11]), .B(B[11]), .SUB(sub), .CARRY_IN(add_sub_11_cout), .result(RESULT[11]), .Cout(add_sub_12_cout));
  ADD_SUB add_sub_13 (
    .A(A[12]), .B(B[12]), .SUB(sub), .CARRY_IN(add_sub_12_cout), .result(RESULT[12]), .Cout(add_sub_13_cout));
  ADD_SUB add_sub_14 (
    .A(A[13]), .B(B[13]), .SUB(sub), .CARRY_IN(add_sub_13_cout), .result(RESULT[13]), .Cout(add_sub_14_cout));
  ADD_SUB add_sub_15 (
    .A(A[14]), .B(B[14]), .SUB(sub), .CARRY_IN(add_sub_14_cout), .result(RESULT[14]), .Cout(add_sub_15_cout));
  ADD_SUB add_sub_16 (.A(A[15]), .B(B[15]), .SUB(sub), .CARRY_IN(add_sub_15_cout), .result(RESULT[15]), .Cout(OVER));
  and and_1 (and_1_out, RESULT[15], sub);
  nand nand_1 (nand_1_out, RESULT[15], OVER);
  nand nand_2 (SLTU[0], RESULT[15], OVER);
  or or_1 (SLTE[0], and_1_out, Zero_flag);
  and and_2 (LESS_FLAG, RESULT[15], sub);
  or or_2 (SLTEU[0], nand_1_out, Zero_flag);
  xor xor_1 (overflow, add_sub_15_cout, OVER);
  or or_3 (or_3_out, RESULT[0], RESULT[1], RESULT[2], RESULT[3], RESULT[4], RESULT[5], RESULT[6], RESULT[7], RESULT[8], RESULT[9], RESULT[10], RESULT[11], RESULT[12], RESULT[13], RESULT[14], RESULT[15]);
  not not_1 (Zero_flag, or_3_out);
  not not_2 (GREAT_FLAG, SLTE[0]);

  assign SLT = {{15{1'b0}}, LESS_FLAG};
  assign SLTE[15:1] = {15{1'b0}};
  assign SLTEU[15:1] = {15{1'b0}};
  assign SLTU[15:1] = {15{1'b0}};

  // Other names for the same wires on the sheet: OR = Zero_flag; r0 = RESULT[0]; r1 = RESULT[1]; r2 = RESULT[2];
  //   r3 = RESULT[3]; r4 = RESULT[4]; r5 = RESULT[5]; r6 = RESULT[6]; r7 = RESULT[7]; r8 = RESULT[8]; r9 = RESULT[9];
  //   r10 = RESULT[10]; r11 = RESULT[11]; r12 = RESULT[12]; r13 = RESULT[13]; r14 = RESULT[14]; r15 = RESULT[15];
  //   SLT_t = RESULT[15]
endmodule

module LOGIC_UNIT (
  input  [15:0] A,
  input  [15:0] B,
  input  [1:0] SELECTOR,
  output [15:0] LOGIC_RESULT
);

  wire [15:0] and_gates_1_and_result, nor_gates_1_nor_result, or_gates_1_or_result, xor_gates_1_xor_result;

  AND_GATES and_gates_1 (.A(A), .B(B), .AND_RESULT(and_gates_1_and_result));
  OR_GATES or_gates_1 (.A(A), .B(A), .OR_RESULT(or_gates_1_or_result));
  NOR_GATES nor_gates_1 (.A(A), .B(A), .NOR_RESULT(nor_gates_1_nor_result));
  XOR_GATES xor_gates_1 (.A(A), .B(A), .XOR_RESULT(xor_gates_1_xor_result));
  Multiplexer #(.select(2), .width(16)) multiplexer_1 (
    .in0(and_gates_1_and_result), .in1(or_gates_1_or_result), .in2(nor_gates_1_nor_result),
    .in3(xor_gates_1_xor_result), .out(LOGIC_RESULT), .sel(SELECTOR));  // open: en
endmodule

module SHIFIT_UNIT (
  input  [3:0] shift_rotate_amount,
  input  [15:0] A,
  input  [1:0] selector,
  output [15:0] result
);

  wire [3:0] s_r;
  wire [15:0] shifter_1_out, shifter_2_out, shifter_3_out, shifter_4_out;

  Shifter #(.width(16)) shifter_1 (.in(A), .\dist (s_r), .out(shifter_1_out));
  Shifter #(.width(16), .shift("lr")) shifter_2 (.in(A), .\dist (s_r), .out(shifter_2_out));
  Shifter #(.width(16), .shift("ar")) shifter_3 (.in(A), .\dist (s_r), .out(shifter_3_out));
  Shifter #(.width(16), .shift("rr")) shifter_4 (.in(A), .\dist (s_r), .out(shifter_4_out));
  Multiplexer #(.select(2), .width(16)) multiplexer_1 (
    .in0(shifter_1_out), .in1(shifter_2_out), .in2(shifter_3_out), .in3(shifter_4_out), .out(result),
    .sel(selector));  // open: en

  // Other names for the same wires on the sheet: s_r_t[3:0] = shift_rotate_amount
endmodule

module ALU_CONTROL (
  input  S5,
  input  S4,
  input  S3,
  input  S2,
  input  S1,
  input  S0,
  output A,
  output B,
  output C
);

  wire and_1_out, and_2_out, and_4_out, and_5_out, not_1_out, not_2_out;

  and and_1 (and_1_out, S3, S1);
  and and_2 (and_2_out, S3, S2);
  not not_1 (not_1_out, S1);
  not not_2 (not_2_out, S3);
  or or_1 (A, and_1_out, and_2_out);
  and and_3 (B, S3, not_1_out);
  and and_4 (and_4_out, not_2_out, S2);
  and and_5 (and_5_out, S3, S0);
  or or_2 (C, and_4_out, and_5_out);
endmodule
