// Logisim project PC_counter.circ as structural Verilog: 1 circuit, main circuit main
module main (
  input  [11:0] Imm12,
  input  JR,
  input  Branch,
  input  CLK,
  input  Reset,
  input  J,
  input  JAL,
  input  JALR,
  input  [15:0] Regester,
  input  [5:0] Imm6,
  output [11:0] out_11
);

  wire or_1_out, or_2_out;
  wire [11:0] adder_1_out, Imm, multiplexer_1_out, multiplexer_2_out, multiplexer_3_out, RS, Rs_t;

  Adder #(.width(12)) adder_1 (.a(out_11), .b(12'h2), .out(adder_1_out));  // open: cin, cout
  Bit_Extender #(.in_width(16), .out_width(12)) bit_extender_1 (.in(Regester), .out(RS));
  assign Imm = {{6{1'b0}}, Imm6};  // Bit_Extender bit_extender_2
  or or_1 (or_1_out, J, JAL);
  Multiplexer #(.width(12)) multiplexer_1 (
    .in0(adder_1_out), .in1(Imm12), .out(multiplexer_1_out), .sel(or_1_out));  // open: en
  or or_2 (or_2_out, JR, JALR);
  Multiplexer #(.width(12)) multiplexer_2 (
    .in0(multiplexer_1_out), .in1(Rs_t), .out(multiplexer_2_out), .sel(or_2_out));  // open: en
  Multiplexer #(.width(12)) multiplexer_3 (
    .in0(multiplexer_2_out), .in1(Imm), .out(multiplexer_3_out), .sel(Branch));  // open: en
  Register #(.width(12)) register_1 (.D(multiplexer_3_out), .Q(out_11), .clk(CLK), .clr(Reset));  // open: en
endmodule
