// Logisim project RegFile_Decoder.circ as structural Verilog: 1 circuit, main circuit main
module main (
  input  [2:0] Rs,
  input  [2:0] Rt,
  input  [2:0] Rd,
  input  [15:0] ALU,
  input  [15:0] Mem,
  input  [11:0] PC,
  input  [11:0] Imm,
  input  JALR,
  input  LUI,
  input  RegDst,
  input  JALR_2,
  input  MemtoReg,
  output [2:0] Rd_2,
  output [15:0] data
);

  wire or_1_out;
  wire [2:0] multiplexer_1_out, multiplexer_3_out;
  wire [11:0] adder_1_out;
  wire [15:0] bit_extender_1_out, Imm_t, multiplexer_2_out, multiplexer_4_out, PC_1;

  assign bit_extender_1_out = {{4{1'b0}}, Imm};  // Bit_Extender bit_extender_1
  Adder #(.width(12)) adder_1 (.a(PC), .b(12'h1), .out(adder_1_out));  // open: cin, cout
  assign PC_1 = {{4{1'b0}}, adder_1_out};  // Bit_Extender bit_extender_2
  Shifter #(.width(16)) shifter_1 (.in(bit_extender_1_out), .\dist (4'b0100), .out(Imm_t));
  Multiplexer #(.width(3)) multiplexer_1 (.in0(Rd), .in1(3'b111), .out(multiplexer_1_out), .sel(JALR));  // open: en
  Multiplexer #(.width(16)) multiplexer_2 (.in0(ALU), .in1(Mem), .out(multiplexer_2_out), .sel(MemtoReg));  // open: en
  Multiplexer #(.width(3)) multiplexer_3 (
    .in0(multiplexer_1_out), .in1(3'b001), .out(multiplexer_3_out), .sel(LUI));  // open: en
  Multiplexer #(.width(16)) multiplexer_4 (
    .in0(multiplexer_2_out), .in1(PC_1), .out(multiplexer_4_out), .sel(or_1_out));  // open: en
  or or_1 (or_1_out, JALR_2, JALR);
  Multiplexer #(.width(3)) multiplexer_5 (.in0(multiplexer_3_out), .in1(Rt), .out(Rd_2), .sel(RegDst));  // open: en
  Multiplexer #(.width(16)) multiplexer_6 (.in0(multiplexer_4_out), .in1(Imm_t), .out(data), .sel(LUI));  // open: en

  // Other names for the same wires on the sheet: JAL = JALR; JALR_t = JALR_2
endmodule
