// Logisim project ALU CONTROL.circ as structural Verilog: 1 circuit, main circuit ALU CONTROL 
module ALU_CONTROL (
  input  [3:0] INPUT,
  input  [1:0] sel,
  input  [3:0] opcode,
  output [1:0] logic_sel,
  output [2:0] ALU_SELECT
);

  wire and_1_out, and_2_out, and_4_out, and_5_out, decoder_1_out6, decoder_1_out7, decoder_1_out8, not_1_out,
       not_2_out, not_3_out, not_4_out, s;
  wire [1:1] and_6_out, not_5_out;
  wire [2:0] multiplexer_2_out, or_3_out;

  Decoder #(.select(4), .enable("false")) decoder_1 (
    .out6(decoder_1_out6), .out7(decoder_1_out7), .out8(decoder_1_out8), .sel(opcode));  // open: out0, out1, out2, out3, out4, out5, out9, out10, out11, out12, out13, out14, out15
  or or_1 (s, decoder_1_out6, decoder_1_out7, decoder_1_out8);
  not not_1 (not_1_out, INPUT[1]);
  not not_2 (not_2_out, INPUT[3]);
  and and_1 (and_1_out, INPUT[3], INPUT[1]);
  or or_2 (or_3_out[2], and_1_out, and_2_out);
  and and_2 (and_2_out, INPUT[3], INPUT[2]);
  and and_3 (or_3_out[1], INPUT[3], not_1_out);
  and and_4 (and_4_out, not_2_out, INPUT[2]);
  and and_5 (and_5_out, INPUT[3], INPUT[0]);
  or or_3 (or_3_out[0], and_4_out, and_5_out);
  not not_3 (not_3_out, opcode[3]);
  not not_4 (not_4_out, opcode[2]);
  not not_5 (not_5_out[1], opcode[2]);
  and and_6 (and_6_out[1], not_3_out, not_4_out);
  Multiplexer #(.width(2), .enable("false")) multiplexer_1 (
    .in0(INPUT[1:0]), .in1({and_6_out[1], opcode[0]}), .out(logic_sel), .sel(s));
  Multiplexer #(.width(3), .enable("false")) multiplexer_2 (
    .in0(or_3_out), .in1({1'b0, not_5_out[1], 1'b0}), .out(multiplexer_2_out), .sel(s));
  Multiplexer #(.select(2), .width(3)) multiplexer_3 (
    .in0(3'b010), .in1(multiplexer_2_out), .out(ALU_SELECT), .sel(sel));  // open: in2, in3, en
endmodule
