// Logisim project CPU.circ as structural Verilog: 1 circuit, main circuit CPU
module CPU (
  input  clear,
  output [15:0] out_2,
  output [15:0] out_3,
  output [15:0] out_4,
  output [15:0] out_5,
  output [15:0] out_6,
  output [15:0] out_7,
  output [15:0] out_8,
  output [15:0] out_9,
  output [15:0] out_10,
  output [11:0] out_11,
  output [15:0] out_12
);

  wire ALU_SRC, B_Z, BEQ, BGEZ, BGT, BGTZ, BLEZ, BLT, BLTZ, BNE, CLK, Great_Flag, J, JAL, JALR, JR,
       Less_Flag, LUI, MEM_READ, MEM_TO_REG, MEM_WR, or_1_out, or_2_out, REG_DST, REG_WR, Zero_Flag;
  wire [1:0] _2_bits_ALU_SEL, ALU_OP;
  wire [2:0] _3_bits_fn, _3_bits_Rd, _3_bits_Rs, _3_bits_Rt, ALU_OPERATION, multiplexer_1_out,
       multiplexer_2_out, multiplexer_4_out, multiplexer_5_out, multiplexer_7_out, multiplexer_8_out;
  wire [3:0] _4_bits_ALU_CON, _4_bits_opcode;
  wire [5:0] _6_bits_immediate;
  wire [11:0] _12_bits_immediate, adder_1_out, NEXT_PC, PC;
  wire [15:0] _6_bits_EXT, _12_bits_EXT, bit_extender_1_out, multiplexer_3_out, multiplexer_9_out, PC_EXT,
       ram_1_data, RD_1, RD_2;
  wire [15:12] ALU_Result;

  Clock clock_1 (.out(CLK));
  Register #(.width(12)) u_PC (.D(NEXT_PC), .Q(PC), .clk(CLK), .clr(clear));  // open: en
  PC pc_2 (
    .PC(PC), ._6_bits_IMM(_6_bits_immediate), ._12_bits_IMM(_12_bits_immediate), .RD_1(RD_1),
    .RESULT(NEXT_PC), .in_13(Less_Flag), .in_5(Great_Flag), .in_12(Zero_Flag), .in_19(BEQ), .in_11(BNE),
    .in_18(BLT), .in_9(BGT), .in_16(BLTZ), .in_10(BLEZ), .in_17(BGTZ), .in_8(BGEZ), .in_15(J), .in_7(JAL),
    .in_14(JR), .in_6(JALR));
  instruction_memory instruction_memory_1 (
    .PC(PC), ._12_bit_immediate(_12_bits_immediate), ._6_bit_immediate(_6_bits_immediate),
    ._4_bit_OpCode(_4_bits_opcode), ._3_bit_Rs(_3_bits_Rs), ._3_bit_Rt(_3_bits_Rt), ._3_bit_Rd(_3_bits_Rd),
    ._3_bit_R_Func(_3_bits_fn), ._4_bits_ALU_con(_4_bits_ALU_CON));
  assign bit_extender_1_out = {{4{_12_bits_immediate[11]}}, _12_bits_immediate};  // Bit_Extender bit_extender_1
  assign _6_bits_EXT = {{10{_6_bits_immediate[5]}}, _6_bits_immediate};  // Bit_Extender bit_extender_2
  Shifter #(.width(16)) shifter_1 (.in(bit_extender_1_out), .\dist (4'b0100), .out(_12_bits_EXT));
  Multiplexer #(.width(3)) multiplexer_1 (
    .in0(_3_bits_Rt), .in1(_3_bits_Rd), .out(multiplexer_1_out), .sel(REG_DST));  // open: en
  Multiplexer #(.width(3)) multiplexer_2 (
    .in0(_3_bits_Rs), .in1(3'b111), .out(multiplexer_2_out), .sel(JR));  // open: en
  Multiplexer #(.width(16)) multiplexer_3 (
    .in0(out_10), .in1(PC_EXT), .out(multiplexer_3_out), .sel(or_1_out));  // open: en
  or or_1 (or_1_out, JALR, JAL);
  Adder #(.width(12)) adder_1 (.a(PC), .b(12'h2), .out(adder_1_out));  // open: cin, cout
  Multiplexer #(.width(3)) multiplexer_4 (
    .in0(multiplexer_1_out), .in1(3'b111), .out(multiplexer_4_out), .sel(JAL));  // open: en
  control_unit control_unit_1 (
    .fn(_3_bits_fn), .ALU_SRC(ALU_SRC), .Branch_Zero(B_Z), .MEM_Read(MEM_READ), .MEM_Write(MEM_WR),
    .MEM_To_Register(MEM_TO_REG), .REG_Write(REG_WR), .REG_DST(REG_DST), .J(J), .JAL(JAL), .JR(JR),
    .JALR(JALR), .BEQ(BEQ), .BNE(BNE), .BLT(BLT), .BGT(BGT), .BLTZ(BLTZ), .BLTEZ(BLEZ), .BGTZ(BGTZ),
    .BGTEZ(BGEZ), .OpCode(_4_bits_opcode), .LUI(LUI), .ALU_OP(ALU_OP), .in_3(_3_bits_Rt));
  assign PC_EXT = {{4{1'b0}}, adder_1_out};  // Bit_Extender bit_extender_3
  Multiplexer #(.width(3)) multiplexer_5 (
    .in0(multiplexer_4_out), .in1(3'b001), .out(multiplexer_5_out), .sel(LUI));  // open: en
  or or_2 (or_2_out, JALR, B_Z, JR);
  Multiplexer #(.width(16)) multiplexer_6 (
    .in0(multiplexer_3_out), .in1(_12_bits_EXT), .out(out_12), .sel(LUI));  // open: en
  Multiplexer #(.width(3)) multiplexer_7 (
    .in0(multiplexer_5_out), .in1(3'b000), .out(multiplexer_7_out), .sel(JR));  // open: en
  Multiplexer #(.width(3)) multiplexer_8 (
    .in0(_3_bits_Rt), .in1(3'b000), .out(multiplexer_8_out), .sel(or_2_out));  // open: en
  Regster_File_main main_1 (
    .Write_Register(multiplexer_7_out), .Read_Register1(multiplexer_2_out), .in_3(multiplexer_8_out),
    .in_4(out_12), .out_7(RD_1), .out_8(RD_2), .in_5(REG_WR), .clock(CLK), .out_9(out_2), .out_10(out_3),
    .out_11(out_4), .out_12(out_5), .out_13(out_6), .out_14(out_7), .out_15(out_8), .out_16(out_9));
  ALU_CONTROL alu_control_1 (
    .ALU_SELECT(ALU_OPERATION), .INPUT(_4_bits_ALU_CON), .sel(ALU_OP), .opcode(_4_bits_opcode),
    .logic_sel(_2_bits_ALU_SEL));
  Multiplexer #(.width(16)) multiplexer_9 (
    .in0(RD_2), .in1(_6_bits_EXT), .out(multiplexer_9_out), .sel(ALU_SRC));  // open: en
  ALU alu_1 (
    .A(RD_1), .B(multiplexer_9_out), .ALU_RESULT({ALU_Result, out_11}), .ZERO_FLAG(Zero_Flag),
    .GREAT_FLAG(Great_Flag), .LESS_FLAG(Less_Flag), .ALU_OPERATION(ALU_OPERATION), .sel(_2_bits_ALU_SEL));  // open: OVER_FLOW_A, OVER_FLOW_S
  RAM #(.addrWidth(12), .dataWidth(16), .bus("separate")) ram_1 (
    .addr(out_11), .din(RD_2), .data(ram_1_data), .str(MEM_WR), .clk(CLK), .ld(MEM_READ));  // open: sel, clr
  Multiplexer #(.width(16)) multiplexer_10 (
    .in0({ALU_Result, out_11}), .in1(ram_1_data), .out(out_10), .sel(MEM_TO_REG));  // open: en

  // Other names for the same wires on the sheet: Adress[11:0] = out_11; ALU_Result[11:0] = out_11; R0[15:0] = out_2;
  //   R1[15:0] = out_3; R2[15:0] = out_4; R3[15:0] = out_5; R4[15:0] = out_6; R5[15:0] = out_7; R6[15:0] = out_8;
  //   R7[15:0] = out_9; Write_Data[15:0] = out_10
endmodule
