// Logisim project FULL ALU.circ as structural Verilog: 9 circuits, main circuit AND GATES
module ALU (
  input  [15:0] A,
  input  [15:0] B,
  input  [2:0] ALU_OPERATION,
  input  [1:0] sel,
  output [15:0] ALU_RESULT,
  output ZERO_FLAG,
  output GREAT_FLAG,
  output LESS_FLAG,
  output OVER_FLOW_A,
  output OVER_FLOW_S
);

  wire [15:0] RES0, RES1, RES2, RES3, SLT, SLTE, SLTEU, SLTU;

  SHIFT_UNIT shift_unit_1 (.shift_rotate_amount(B[3:0]), .A(A), .result(RES1), .selector(sel));
  LOGIC_UNIT logic_unit_1 (.A(A), .B(B), .LOGIC_RESULT(RES0), .SELECTOR(sel));
  ARITHMATIC_UNIT arithmatic_unit_1 (
    .A(A), .B(B), .RESULT_1(RES2), .Zero_flag(ZERO_FLAG), .SLTEU(SLTEU), .SLTU(SLTU),
    .GREAT_FLAG(GREAT_FLAG), .SLTE(SLTE), .LESS_FLAG(LESS_FLAG), .SLT(SLT), .overflow_2(OVER_FLOW_S),
    .RESULT_2(RES3), .overflow_1(OVER_FLOW_A));
  Multiplexer #(.select(3), .width(16)) multiplexer_1 (
    .in0(RES0), .in1(RES1), .in2(RES2), .in3(RES3), .in4(SLT), .in5(SLTU), .in6(SLTE), .in7(SLTEU),
    .out(ALU_RESULT), .sel(ALU_OPERATION));  // open: en

  // Other names for the same wires on the sheet: SHIFT_ROTAT[3:0] = B[3:0]
endmodule

// 16_BITS AND
module AND_GATES (
  input  [15:0] A,
  input  [15:0] B,
  output [15:0] AND_RESULT
);

  and and_1 (AND_RESULT[0], A[0], B[0]);
  and and_2 (AND_RESULT[1], A[1], B[1]);
  and and_3 (AND_RESULT[2], A[2], B[2]);
  and and_4 (AND_RESULT[3], A[3], B[3]);
  and and_5 (AND_RESULT[4], A[4], B[4]);
  and and_6 (AND_RESULT[5], A[5], B[5]);
  and and_7 (AND_RESULT[6], A[6], B[6]);
  and and_8 (AND_RESULT[7], A[7], B[7]);
  and and_9 (AND_RESULT[8], A[8], B[8]);
  and and_10 (AND_RESULT[9], A[9], B[9]);
  and and_11 (AND_RESULT[10], A[10], B[10]);
  and and_12 (AND_RESULT[11], A[11], B[11]);
  and and_13 (AND_RESULT[12], A[12], B[12]);
  and and_14 (AND_RESULT[13], A[13], B[13]);
  and and_15 (AND_RESULT[14], A[14], B[14]);
  and and_16 (AND_RESULT[15], A[15], B[15]);
endmodule

// 16_BITS OR
module OR_GATES (
  input  [15:0] A,
  input  [15:0] B,
  output [15:0] OR_RESULT
);

  or or_1 (OR_RESULT[0], A[0], B[0]);
  or or_2 (OR_RESULT[1], A[1], B[1]);
  or or_3 (OR_RESULT[2], A[2], B[2]);
  or or_4 (OR_RESULT[3], A[3], B[3]);
  or or_5 (OR_RESULT[4], A[4], B[4]);
  or or_6 (OR_RESULT[5], A[5], B[5]);
  or or_7 (OR_RESULT[6], A[6], B[6]);
  or or_8 (OR_RESULT[7], A[7], B[7]);
  or or_9 (OR_RESULT[8], A[8], B[8]);
  or or_10 (OR_RESULT[9], A[9], B[9]);
  or or_11 (OR_RESULT[10], A[10], B[10]);
  or or_12 (OR_RESULT[11], A[11], B[11]);
  or or_13 (OR_RESULT[12], A[12], B[12]);
  or or_14 (OR_RESULT[13], A[13], B[13]);
  or or_15 (OR_RESULT[14], A[14], B[14]);
  or or_16 (OR_RESULT[15], A[15], B[15]);
endmodule

// 16_BITS XOR
module XOR_GATES (
  input  [15:0] A,
  input  [15:0] B,
  output [15:0] XOR_RESULT
);

  xor xor_1 (XOR_RESULT[0], A[0], B[0]);
  xor xor_2 (XOR_RESULT[1], A[1], B[1]);
  xor xor_3 (XOR_RESULT[2], A[2], B[2]);
  xor xor_4 (XOR_RESULT[3], A[3], B[3]);
  xor xor_5 (XOR_RESULT[4], A[4], B[4]);
  xor xor_6 (XOR_RESULT[5], A[5], B[5]);
  xor xor_7 (XOR_RESULT[6], A[6], B[6]);
  xor xor_8 (XOR_RESULT[7], A[7], B[7]);
  xor xor_9 (XOR_RESULT[8], A[8], B[8]);
  xor xor_10 (XOR_RESULT[9], A[9], B[9]);
  xor xor_11 (XOR_RESULT[10], A[10], B[10]);
  xor xor_12 (XOR_RESULT[11], A[11], B[11]);
  xor xor_13 (XOR_RESULT[12], A[12], B[12]);
  xor xor_14 (XOR_RESULT[13], A[13], B[13]);
  xor xor_15 (XOR_RESULT[14], A[14], B[14]);
  xor xor_16 (XOR_RESULT[15], A[15], B[15]);
endmodule

// 16_BITS NOR
module NOR_GATES (
  input  [15:0] A,
  input  [15:0] B,
  output [15:0] NOR_RESULT
);

  nor nor_1 (NOR_RESULT[0], A[0], B[0]);
  nor nor_2 (NOR_RESULT[1], A[1], B[1]);
  nor nor_3 (NOR_RESULT[2], A[2], B[2]);
  nor nor_4 (NOR_RESULT[3], A[3], B[3]);
  nor nor_5 (NOR_RESULT[4], A[4], B[4]);
  nor nor_6 (NOR_RESULT[5], A[5], B[5]);
  nor nor_7 (NOR_RESULT[6], A[6], B[6]);
  nor nor_8 (NOR_RESULT[7], A[7], B[7]);
  nor nor_9 (NOR_RESULT[8], A[8], B[8]);
  nor nor_10 (NOR_RESULT[9], A[9], B[9]);
  nor nor_11 (NOR_RESULT[10], A[10], B[10]);
  nor nor_12 (NOR_RESULT[11], A[11], B[11]);
  nor nor_13 (NOR_RESULT[12], A[12], B[12]);
  nor nor_14 (NOR_RESULT[13], A[13], B[13]);
  nor nor_15 (NOR_RESULT[14], A[14], B[14]);
  nor nor_16 (NOR_RESULT[15], A[15], B[15]);
endmodule

module ADD_SUB (
  input  A,
  input  B,
  input  CARRY_IN_1,
  input  CARRY_IN_2,
  output result2,
  output C_out1,
  output result1,
  output Cout_2
);

  Adder #(.width(1)) adder_1 (.a(A), .b(B), .out(result2), .cin(CARRY_IN_1), .cout(C_out1));
  Subtractor #(.width(1)) subtractor_1 (.a(A), .b(B), .out(result1), .bin(CARRY_IN_2), .bout(Cout_2));

  // Other names for the same wires on the sheet: Cin_1 = CARRY_IN_1; Cin_2 = CARRY_IN_2
endmodule

module ARITHMATIC_UNIT (
  input  [15:0] A,
  input  [15:0] B,
  output [15:0] RESULT_1,
  output [15:0] RESULT_2,
  output Zero_flag,
  output [15:0] SLTEU,
  output [15:0] SLTU,
  output GREAT_FLAG,
  output [15:0] SLTE,
  output LESS_FLAG,
  output [15:0] SLT,
  output overflow_2,
  output overflow_1
);

  wire add_sub_1_c_out1, add_sub_1_cout_2, add_sub_2_c_out1, add_sub_2_cout_2, add_sub_3_c_out1,
       add_sub_3_cout_2, add_sub_4_c_out1, add_sub_4_cout_2, add_sub_5_c_out1, add_sub_5_cout_2,
       add_sub_6_c_out1, add_sub_6_cout_2, add_sub_7_c_out1, add_sub_7_cout_2, add_sub_8_c_out1,
       add_sub_8_cout_2, add_sub_9_c_out1, add_sub_9_cout_2, add_sub_10_c_out1, add_sub_10_cout_2,
       add_sub_11_c_out1, add_sub_11_cout_2, add_sub_12_c_out1, add_sub_12_cout_2, add_sub_13_c_out1,
       add_sub_13_cout_2, add_sub_14_c_out1, add_sub_14_cout_2, add_sub_15_c_out1, add_sub_15_cout_2,
       add_sub_16_c_out1, add_sub_16_cout_2, GREAT, GREATU, ZEROU;

  Comparator #(.width(16)) comparator_1 (.a(A), .b(B), .gt(GREAT), .eq(Zero_flag), .lt(LESS_FLAG));
  Comparator #(.width(16), .mode("unsigned")) comparator_2 (.a(A), .b(B), .gt(GREATU), .eq(ZEROU), .lt(SLTU[0]));
  ADD_SUB add_sub_1 (
    .A(A[0]), .B(B[0]), .result2(RESULT_1[0]), .C_out1(add_sub_1_c_out1), .result1(RESULT_2[0]),
    .Cout_2(add_sub_1_cout_2), .CARRY_IN_1(1'b0), .CARRY_IN_2(1'b0));
  ADD_SUB add_sub_2 (
    .A(A[1]), .B(B[1]), .result2(RESULT_1[1]), .C_out1(add_sub_2_c_out1), .result1(RESULT_2[1]),
    .Cout_2(add_sub_2_cout_2), .CARRY_IN_1(add_sub_1_c_out1), .CARRY_IN_2(add_sub_1_cout_2));
  ADD_SUB add_sub_3 (
    .A(A[2]), .B(B[2]), .result2(RESULT_1[2]), .C_out1(add_sub_3_c_out1), .result1(RESULT_2[2]),
    .Cout_2(add_sub_3_cout_2), .CARRY_IN_1(add_sub_2_c_out1), .CARRY_IN_2(add_sub_2_cout_2));
  ADD_SUB add_sub_4 (
    .A(A[3]), .B(B[3]), .result2(RESULT_1[3]), .C_out1(add_sub_4_c_out1), .result1(RESULT_2[3]),
    .Cout_2(add_sub_4_cout_2), .CARRY_IN_1(add_sub_3_c_out1), .CARRY_IN_2(add_sub_3_cout_2));
  ADD_SUB add_sub_5 (
    .A(A[4]), .B(B[4]), .result2(RESULT_1[4]), .C_out1(add_sub_5_c_out1), .result1(RESULT_2[4]),
    .Cout_2(add_sub_5_cout_2), .CARRY_IN_1(add_sub_4_c_out1), .CARRY_IN_2(add_sub_4_cout_2));
  ADD_SUB add_sub_6 (
    .A(A[5]), .B(B[5]), .result2(RESULT_1[5]), .C_out1(add_sub_6_c_out1), .result1(RESULT_2[5]),
    .Cout_2(add_sub_6_cout_2), .CARRY_IN_1(add_sub_5_c_out1), .CARRY_IN_2(add_sub_5_cout_2));
  ADD_SUB add_sub_7 (
    .A(A[6]), .B(B[6]), .result2(RESULT_1[6]), .C_out1(add_sub_7_c_out1), .result1(RESULT_2[6]),
    .Cout_2(add_sub_7_cout_2), .CARRY_IN_1(add_sub_6_c_out1), .CARRY_IN_2(add_sub_6_cout_2));
  ADD_SUB add_sub_8 (
    .A(A[7]), .B(B[7]), .result2(RESULT_1[7]), .C_out1(add_sub_8_c_out1), .result1(RESULT_2[7]),
    .Cout_2(add_sub_8_cout_2), .CARRY_IN_1(add_sub_7_c_out1), .CARRY_IN_2(add_sub_7_cout_2));
  ADD_SUB add_sub_9 (
    .A(A[8]), .B(B[8]), .result2(RESULT_1[8]), .C_out1(add_sub_9_c_out1), .result1(RESULT_2[8]),
    .Cout_2(add_sub_9_cout_2), .CARRY_IN_1(add_sub_8_c_out1), .CARRY_IN_2(add_sub_8_cout_2));
  ADD_SUB add_sub_10 (
    .A(A[9]), .B(B[9]), .result2(RESULT_1[9]), .C_out1(add_sub_10_c_out1), .result1(RESULT_2[9]),
    .Cout_2(add_sub_10_cout_2), .CARRY_IN_1(add_sub_9_c_out1), .CARRY_IN_2(add_sub_9_cout_2));
  ADD_SUB add_sub_11 (
    .A(A[10]), .B(B[10]), .result2(RESULT_1[10]), .C_out1(add_sub_11_c_out1), .result1(RESULT_2[10]),
    .Cout_2(add_sub_11_cout_2), .CARRY_IN_1(add_sub_10_c_out1), .CARRY_IN_2(add_sub_10_cout_2));
  ADD_SUB add_sub_12 (
    .A(A[11]), .B(B[11]), .result2(RESULT_1[11]), .C_out1(add_sub_12_c_out1), .result1(RESULT_2[11]),
    .Cout_2(add_sub_12_cout_2), .CARRY_IN_1(add_sub_11_c_out1), .CARRY_IN_2(add_sub_11_cout_2));
  ADD_SUB add_sub_13 (
    .A(A[12]), .B(B[12]), .result2(RESULT_1[12]), .C_out1(add_sub_13_c_out1), .result1(RESULT_2[12]),
    .Cout_2(add_sub_13_cout_2), .CARRY_IN_1(add_sub_12_c_out1), .CARRY_IN_2(add_sub_12_cout_2));
  ADD_SUB add_sub_14 (
    .A(A[13]), .B(B[13]), .result2(RESULT_1[13]), .C_out1(add_sub_14_c_out1), .result1(RESULT_2[13]),
    .Cout_2(add_sub_14_cout_2), .CARRY_IN_1(add_sub_13_c_out1), .CARRY_IN_2(add_sub_13_cout_2));
  ADD_SUB add_sub_15 (
    .A(A[14]), .B(B[14]), .result2(RESULT_1[14]), .C_out1(add_sub_15_c_out1), .result1(RESULT_2[14]),
    .Cout_2(add_sub_15_cout_2), .CARRY_IN_1(add_sub_14_c_out1), .CARRY_IN_2(add_sub_14_cout_2));
  ADD_SUB add_sub_16 (
    .A(A[15]), .B(B[15]), .result2(RESULT_1[15]), .C_out1(add_sub_16_c_out1), .result1(RESULT_2[15]),
    .Cout_2(add_sub_16_cout_2), .CARRY_IN_1(add_sub_15_c_out1), .CARRY_IN_2(add_sub_15_cout_2));
  or or_1 (SLTE[0], LESS_FLAG, Zero_flag);
  xor xor_1 (overflow_1, add_sub_15_c_out1, add_sub_16_c_out1);
  or or_2 (SLTEU[0], SLTU[0], Zero_flag);
  xor xor_2 (overflow_2, add_sub_15_cout_2, add_sub_16_cout_2);
  not not_1 (GREAT_FLAG, SLTE[0]);

  assign SLT = {{15{1'b0}}, LESS_FLAG};
  assign SLTE[15:1] = {15{1'b0}};
  assign SLTEU[15:1] = {15{1'b0}};
  assign SLTU[15:1] = {15{1'b0}};

  // Other names for the same wires on the sheet: r0_t = RESULT_1[0]; r1_t = RESULT_1[1]; r2_t = RESULT_1[2];
  //   r3_t = RESULT_1[3]; r4_t = RESULT_1[4]; r5_t = RESULT_1[5]; r6_t = RESULT_1[6]; r7_t = RESULT_1[7];
  //   r8_t = RESULT_1[8]; r9_t = RESULT_1[9]; r10_t = RESULT_1[10]; r11_t = RESULT_1[11]; r12_t = RESULT_1[12];
  //   r13_t = RESULT_1[13]; r14_t = RESULT_1[14]; r15_t = RESULT_1[15]; R0 = RESULT_2[0]; R1 = RESULT_2[1];
  //   R2 = RESULT_2[2]; R3 = RESULT_2[3]; R4 = RESULT_2[4]; R5 = RESULT_2[5]; R6 = RESULT_2[6]; R7 = RESULT_2[7];
  //   R8 = RESULT_2[8]; R9 = RESULT_2[9]; R10 = RESULT_2[10]; R11 = RESULT_2[11]; R12 = RESULT_2[12];
  //   R13 = RESULT_2[13]; R14 = RESULT_2[14]; R15 = RESULT_2[15]; SLT_t = LESS_FLAG; SLTU_t = SLTU[0]; OR = Zero_flag;
  //   ZERO = Zero_flag
endmodule

module LOGIC_UNIT (
  input  [15:0] A,
  input  [15:0] B,
  input  [1:0] SELECTOR,
  output [15:0] LOGIC_RESULT
);

  wire [15:0] and_gates_1_and_result, nor_gates_1_nor_result, or_gates_1_or_result, xor_gates_1_xor_result;

  AND_GATES and_gates_1 (.A(A), .B(B), .AND_RESULT(and_gates_1_and_result));
  OR_GATES or_gates_1 (.A(A), .B(B), .OR_RESULT(or_gates_1_or_result));
  NOR_GATES nor_gates_1 (.A(A), .B(B), .NOR_RESULT(nor_gates_1_nor_result));
  XOR_GATES xor_gates_1 (.A(A), .B(B), .XOR_RESULT(xor_gates_1_xor_result));
  Multiplexer #(.select(2), .width(16)) multiplexer_1 (
    .in0(and_gates_1_and_result), .in1(or_gates_1_or_result), .in2(nor_gates_1_nor_result),
    .in3(xor_gates_1_xor_result), .out(LOGIC_RESULT), .sel(SELECTOR));  // open: en
endmodule

// SHIFT UNT
module SHIFT_UNIT (
  input  [3:0] shift_rotate_amount,
  input  [15:0] A,
  input  [1:0] selector,
  output [15:0] result
);

  wire [3:0] s_r;
  wire [15:0] shifter_1_out, shifter_2_out, shifter_3_out, shifter_4_out;

  Shifter #(.width(16)) shifter_1 (.in(A), .\dist (s_r), .out(shifter_1_out));
  Shifter #(.width(16), .shift("lr")) shifter_2 (.in(A), .\dist (s_r), .out(shifter_2_out));
  Shifter #(.width(16), .shift("ar")) shifter_3 (.in(A), .\dist (s_r), .out(shifter_3_out));
  Shifter #(.width(16), .shift("rr")) shifter_4 (.in(A), .\dist (s_r), .out(shifter_4_out));
  Multiplexer #(.select(2), .width(16)) multiplexer_1 (
    .in0(shifter_1_out), .in1(shifter_2_out), .in2(shifter_3_out), .in3(shifter_4_out), .out(result),
    .sel(selector));  // open: en

  // Other names for the same wires on the sheet: s_r_t[3:0] = shift_rotate_amount
endmodule
