// Logisim project instruction memory.circ as structural Verilog: 1 circuit, main circuit instruction memory
module instruction_memory (
  input  [11:0] PC,
  output [11:0] _12_bit_immediate,
  output [5:0] _6_bit_immediate,
  output [3:0] _4_bit_OpCode,
  output [2:0] _3_bit_Rs,
  output [2:0] _3_bit_Rt,
  output [2:0] _3_bit_Rd,
  output [2:0] _3_bit_R_Func,
  output [3:0] _4_bits_ALU_con
);

  ROM #(.addrWidth(12), .dataWidth(16)) rom_1 (
    .addr(PC), .data({_4_bit_OpCode, _3_bit_Rs, _3_bit_Rt, _3_bit_Rd, _3_bit_R_Func}));  // open: sel

  assign _4_bits_ALU_con = {_4_bit_OpCode[0], _3_bit_R_Func};
  assign _6_bit_immediate = {_3_bit_Rd, _3_bit_R_Func};
  assign _12_bit_immediate = {_3_bit_Rs, _3_bit_Rt, _3_bit_Rd, _3_bit_R_Func};

  // Other names for the same wires on the sheet: _13 = _4_bit_OpCode[1]; _14 = _4_bit_OpCode[2];
  //   _15 = _4_bit_OpCode[3]; _12 = _4_bit_OpCode[0]; _0 = _3_bit_R_Func[0]; _1 = _3_bit_R_Func[1];
  //   _2 = _3_bit_R_Func[2]; _3 = _3_bit_Rd[0]; _4 = _3_bit_Rd[1]; _5 = _3_bit_Rd[2]; _6 = _3_bit_Rt[0];
  //   _7 = _3_bit_Rt[1]; _8 = _3_bit_Rt[2]; _9 = _3_bit_Rs[0]; _10 = _3_bit_Rs[1]; _11 = _3_bit_Rs[2]

  // Notes on the sheet:
  //   Instruction Memory
endmodule
