// Logisim project control unit.circ as structural Verilog: 5 circuits, main circuit main
module main (
  input  [3:0] in_1,
  input  [2:0] \function ,
  input  Z_F,
  input  Great_F,
  input  Less_F,
  input  [2:0] Rt,
  output RegDst,
  output MemRead,
  output RegWrite,
  output MemtoReg,
  output MemWrite,
  output ALUOp,
  output ALUSrc,
  output LUI,
  output R2,
  output Jump,
  output R1,
  output JR,
  output R0,
  output JALR,
  output JAL,
  output Branch
);

  wire op_decoder_1_regwrite;

  // ALU_CONTROL alu_control_1: pin names not known; wires that end beside it: in_1[3], in_1[2], in_1[1], in_1[0], \function [2], \function [1], R2, R1, R0
  op_decoder op_decoder_1 (
    .OP3(in_1[3]), .RegDst(RegDst), .OP2(in_1[2]), .OP1(in_1[1]), .MemRead(MemRead), .OP0(in_1[0]),
    .MemtoReg(MemtoReg), .MemWrite(MemWrite), .ALUOp(ALUOp), .ALUSrc(ALUSrc),
    .RegWrite(op_decoder_1_regwrite), .LUI(LUI));
  jump_decoder jump_decoder_1 (
    .op3(in_1[3]), .jump(Jump), .op2(in_1[2]), .op1(in_1[1]), .JR(JR), .op0(in_1[0]), .f2(\function [2]),
    .f1(\function [1]), .JALR(JALR), .f0(\function [0]), .JAL(JAL));
  Branch_decoder branch_decoder_1 (
    .OP3(in_1[3]), .OP2(in_1[2]), .OP1(in_1[1]), .OP0(in_1[0]), .Rt(Rt[0]), .in_7(Z_F), .in_6(Great_F),
    .in_8(Less_F), .Branch(Branch));
  RegDst regdst_1 (
    .RegWrite(op_decoder_1_regwrite), .f2(\function [2]), .RegWrite_2(RegWrite), .f1(\function [1]),
    .f0(\function [0]));

  // Other names for the same wires on the sheet: f0 = \function [0]; f1 = \function [1]; f2 = \function [2];
  //   op0 = in_1[0]; op1 = in_1[1]; op2 = in_1[2]; op3 = in_1[3]

  // Notes on the sheet:
  //   opcode
endmodule

module op_decoder (
  input  OP3,
  input  OP2,
  input  OP1,
  input  OP0,
  output RegDst,
  output MemRead,
  output MemtoReg,
  output MemWrite,
  output ALUOp,
  output ALUSrc,
  output RegWrite,
  output LUI
);

  wire and_1_out, and_2_out, and_4_out, and_5_out, and_6_out, and_7_out, and_8_out, and_9_out, and_10_out,
       and_11_out, not_1_out, not_2_out, not_3_out, not_4_out, not_5_out, not_6_out, not_7_out, not_8_out,
       not_9_out, not_10_out, not_11_out, not_12_out, not_13_out, not_14_out, not_15_out, not_16_out,
       not_17_out, not_18_out, not_19_out, not_20_out, not_21_out, not_22_out, not_23_out, not_24_out,
       not_25_out, not_26_out;

  not not_1 (not_1_out, OP3);
  and and_1 (and_1_out, not_1_out, not_2_out);
  not not_2 (not_2_out, OP1);
  and and_2 (and_2_out, OP3, OP1);
  not not_3 (not_3_out, OP3);
  not not_4 (not_4_out, OP2);
  not not_5 (not_5_out, OP0);
  not not_6 (not_6_out, OP2);
  and and_3 (MemtoReg, not_6_out, OP1);
  not not_7 (not_7_out, OP3);
  not not_8 (not_8_out, OP2);
  not not_9 (not_9_out, OP3);
  not not_10 (not_10_out, OP1);
  and and_4 (and_4_out, not_10_out, not_11_out);
  not not_11 (not_11_out, OP0);
  and and_5 (and_5_out, OP2, not_12_out);
  not not_12 (not_12_out, OP1);
  not not_13 (not_13_out, OP3);
  and and_6 (and_6_out, not_13_out, OP1);
  and and_7 (and_7_out, OP3, not_14_out);
  not not_14 (not_14_out, OP2);
  not not_15 (not_15_out, OP3);
  and and_8 (and_8_out, not_15_out, not_16_out, not_17_out);
  not not_16 (not_16_out, OP2);
  not not_17 (not_17_out, OP1);
  not not_18 (not_18_out, OP3);
  not not_19 (not_19_out, OP2);
  and and_9 (and_9_out, not_18_out, not_19_out, not_20_out);
  not not_20 (not_20_out, OP0);
  not not_21 (not_21_out, OP2);
  and and_10 (and_10_out, not_21_out, not_22_out, not_23_out);
  not not_22 (not_22_out, OP1);
  not not_23 (not_23_out, OP0);
  not not_24 (not_24_out, OP3);
  and and_11 (and_11_out, not_24_out, OP2, OP1);
  or or_1 (RegDst, and_1_out, and_2_out);
  and and_12 (MemRead, not_3_out, not_4_out, OP1, not_5_out);
  and and_13 (MemWrite, not_7_out, not_8_out, OP1, OP0);
  or or_2 (ALUOp, not_9_out, and_4_out, and_5_out);
  or or_3 (ALUSrc, and_6_out, and_7_out);
  or or_4 (RegWrite, and_8_out, and_9_out, and_10_out, and_11_out);
  not not_25 (not_25_out, OP0);
  and and_14 (LUI, not_25_out, OP1, not_26_out, OP3);
  not not_26 (not_26_out, OP2);
endmodule

module jump_decoder (
  input  op3,
  input  op2,
  input  op1,
  input  op0,
  input  f2,
  input  f1,
  input  f0,
  output jump,
  output JR,
  output JALR,
  output JAL
);

  wire not_1_out, not_2_out, not_3_out, not_4_out, not_5_out, not_6_out, not_7_out, not_8_out, not_9_out,
       not_10_out;

  not not_1 (not_1_out, op2);
  not not_2 (not_2_out, op1);
  not not_3 (not_3_out, op3);
  not not_4 (not_4_out, op2);
  not not_5 (not_5_out, op1);
  not not_6 (not_6_out, f0);
  not not_7 (not_7_out, op3);
  not not_8 (not_8_out, op2);
  not not_9 (not_9_out, op1);
  not not_10 (not_10_out, op2);
  and and_1 (jump, op3, not_1_out, not_2_out, op0);
  and and_2 (JR, not_3_out, not_4_out, not_5_out, op0, f2, f1, not_6_out);
  and and_3 (JALR, not_7_out, not_8_out, not_9_out, op0, f2, f1, f0);
  and and_4 (JAL, not_10_out, op1, op0, op3);
endmodule

module Branch_decoder (
  input  OP3,
  input  OP2,
  input  OP1,
  input  OP0,
  input  Rt,
  input  in_6,
  input  in_7,
  input  in_8,
  output Branch
);

  wire and_7_out, and_8_out, and_9_out, and_10_out, and_11_out, and_12_out, and_13_out, and_14_out, BEQ, BGT,
       BGZ, BLT, BLZ, BNE, not_1_out, not_2_out, not_3_out, not_4_out, not_5_out, not_6_out, not_7_out,
       not_8_out, not_9_out, not_10_out, not_11_out, not_12_out, or_1_out, or_2_out;

  not not_1 (not_1_out, OP3);
  not not_2 (not_2_out, OP1);
  not not_3 (not_3_out, OP0);
  not not_4 (not_4_out, OP3);
  not not_5 (not_5_out, OP1);
  not not_6 (not_6_out, OP1);
  and and_1 (BGT, OP3, OP2, OP1, OP0);
  not not_7 (not_7_out, OP1);
  not not_8 (not_8_out, OP0);
  not not_9 (not_9_out, OP0);
  and and_2 (BEQ, not_1_out, OP2, not_2_out, not_3_out);
  and and_3 (BNE, not_4_out, OP2, not_5_out, OP0);
  and and_4 (BLT, OP3, OP2, not_6_out, OP0);
  and and_5 (BLZ, OP3, OP2, not_7_out, not_8_out);
  and and_6 (BGZ, OP3, OP2, OP1, not_9_out);
  or or_1 (or_1_out, in_6, in_8);
  or or_2 (or_2_out, in_6, in_7);
  not not_10 (not_10_out, Rt);
  not not_11 (not_11_out, Rt);
  and and_7 (and_7_out, BEQ, in_6);
  not not_12 (not_12_out, in_6);
  and and_8 (and_8_out, not_12_out, BNE);
  and and_9 (and_9_out, BGZ, not_10_out, in_7);
  and and_10 (and_10_out, in_7, BGT);
  and and_11 (and_11_out, BLZ, not_11_out, in_8);
  and and_12 (and_12_out, in_8, BLT);
  and and_13 (and_13_out, Rt, BLZ, or_1_out);
  and and_14 (and_14_out, Rt, BGZ, or_2_out);
  or or_3 (Branch, and_7_out, and_8_out, and_9_out, and_10_out, and_11_out, and_12_out, and_13_out, and_14_out);

  // Other names for the same wires on the sheet: Great_F = in_7; Less_F = in_8; Z_F = in_6
endmodule

module RegDst (
  input  RegWrite,
  input  f2,
  input  f1,
  input  f0,
  output RegWrite_2
);

  wire and_1_out, and_2_out, and_3_out, not_1_out, not_2_out;

  and and_1 (and_1_out, RegWrite, not_1_out);
  not not_1 (not_1_out, f2);
  and and_2 (and_2_out, RegWrite, not_2_out);
  not not_2 (not_2_out, f1);
  and and_3 (and_3_out, RegWrite, f0);
  or or_1 (RegWrite_2, and_1_out, and_2_out, and_3_out);
endmodule
