// Logisim project CONTROL UNIT.circ as structural Verilog: 1 circuit, main circuit control unit
module control_unit (
  input  [3:0] OpCode,
  input  [2:0] fn,
  input  [2:0] in_3,
  output ALU_SRC,
  output [1:0] ALU_OP,
  output out_6,
  output Branch_Zero,
  output MEM_Read,
  output MEM_Write,
  output MEM_To_Register,
  output out_11,
  output REG_Write,
  output REG_DST,
  output J,
  output JAL,
  output JR,
  output JALR,
  output BEQ,
  output LUI,
  output BNE,
  output BLT,
  output BGT,
  output BLTZ,
  output BLTEZ,
  output BGTZ,
  output BGTEZ
);

  wire _0, _1, _6, _7, _8, _12, _14, and_1_out, and_2_out, E, F, not_1_out, or_2_out;

  Decoder #(.select(4), .enable("false")) decoder_1 (
    .out0(_0), .out1(_1), .out2(MEM_Read), .out3(MEM_Write), .out4(BEQ), .out5(BNE), .out6(_6), .out7(_7),
    .out8(_8), .out9(J), .out10(LUI), .out11(JAL), .out12(_12), .out13(BLT), .out14(_14), .out15(BGT),
    .sel(OpCode));
  Decoder #(.select(3), .enable("false")) decoder_2 (
    .out0(E), .out1(F), .sel(in_3));  // open: out2, out3, out4, out5, out6, out7
  not not_1 (not_1_out, fn[0]);
  and and_1 (and_1_out, fn[2], fn[1], fn[0]);
  and and_2 (and_2_out, fn[2], fn[1], not_1_out);
  or or_1 (out_6, _0, _1);
  and and_3 (JALR, and_1_out, _1);
  and and_4 (JR, and_2_out, _1);
  or or_2 (or_2_out, MEM_Read, MEM_Write);
  or or_3 (ALU_OP[1], J, LUI, JAL);
  not not_2 (ALU_OP[0], or_2_out);
  or or_4 (out_11, MEM_Read, _6, _7, _8);
  or or_5 (ALU_SRC, MEM_Read, MEM_Write, _6, _7, _8);
  and and_5 (BLTZ, E, _12);
  and and_6 (BGTZ, _14, E);
  or or_6 (Branch_Zero, _12, _14);
  and and_7 (BLTEZ, F, _12);
  and and_8 (BGTEZ, F, _14);
  or or_7 (REG_Write, JAL, out_6, LUI, out_11);

  assign MEM_To_Register = MEM_Read;
  assign REG_DST = out_6;

  // Other names for the same wires on the sheet: _2 = MEM_Read; _3 = MEM_Write; _4 = BEQ; _5 = BNE; _9 = J; _10 = LUI;
  //   _11 = JAL; _13 = BLT; _15 = BGT; SS = ALU_OP[0]; HH = ALU_OP[1]; I_TYPE = out_11; R_type = out_6
endmodule
