// Logisim project CPU3.circ as structural Verilog: 7 circuits, main circuit CPU
module CPU (
  input  clear,
  output [15:0] out_2,
  output [15:0] out_3,
  output [15:0] out_4,
  output [15:0] out_5,
  output [15:0] out_6,
  output [15:0] out_7,
  output [15:0] out_8,
  output [15:0] out_9,
  output [2:0] out_10,
  output [27:0] out_11,
  output [15:0] out_12,
  output [11:0] out_13,
  output [15:0] out_14
);

  wire ALU_SRC, ALU_SRC_2, ALU_SRC_3, B_Z, BEQ, BEQ2, BEQ3, BGEZ, BGEZ2, BGEZ3, BGT, BGT2, BGT3, BGTZ, BGTZ2,
       BGTZ3, BLEZ, BLEZ2, BLEZ3, BLT, BLT2, BLT3, BLTZ, BLTZ2, BLTZ3, BNE, BNE2, BNE3, Branch_flush, CLK,
       EQ, Forword_sw, G, Great_Flag, I, Jump_flush, L, Less_Flag, LUI, multiplexer_10_out, not_1_out,
       not_2_out, or_1_out, or_2_out, or_3_out, or_4_out, or_5_out, R, stall, Zero_Flag;
  wire [1:0] _2_bits_ALU_SEL, ALU_OP, ALU_OP_2, ALU_OP_3, Forword_A, Forword_B;
  wire [2:0] _3_bits_fn, _3_bits_fn_1, _3_bits_Rd, _3_bits_Rd_1, _3_bits_Rd_2, _3_bits_Rd_3, _3_bits_Rs,
       _3_bits_Rs_1, _3_bits_Rs_2, _3_bits_Rt, _3_bits_Rt_1, _3_bits_Rt_2, ALU_OPERATION, multiplexer_4_out,
       multiplexer_6_out, multiplexer_7_out, multiplexer_9_out, Ra, RD, RD1, RD2;
  wire [3:0] _4_bits_ALU_CON, _4_bits_opcode, _4_bits_opcode_1_t;
  wire [5:0] _6_bits_immediate, _6_bits_immediate_1;
  wire [11:0] _12_bits_immediate, _12_bits_immediate_1, adder_1_out, NEXT_PC, PC, PC_1, PC_2, PC_if_id;
  wire [15:0] _6_bits_EXT, _12_bits_EXT, ALU_out, bit_extender_2_out, Bus_A, Bus_A_1, Bus_A_2, Bus_B,
       Bus_B_1, Bus_B_2, data1, data2, data_1, Ins, Mem, mem_wb_1_alu_out_2, mem_wb_1_mem_out_2,
       multiplexer_1_out, multiplexer_3_out, multiplexer_12_out, multiplexer_13_out, PC_EXT, rom_1_data;
  wire [15:12] ALU_Result;
  wire [27:0] multiplexer_11_out;
  wire [27:2] control_signal, control_signal_2, control_signal_3;

  PC u_pc_1 (
    .PC(PC), ._12_bits_IMM(_12_bits_immediate), .RD_1(data1), .RESULT(NEXT_PC), .in_13(L), .in_5(G),
    .in_12(EQ), .in_19(BEQ), .in_11(BNE), .in_18(BLT), .in_9(BGT), .in_16(BLTZ), .in_10(BLEZ), .in_17(BGTZ),
    .in_8(BGEZ), .in_15(control_signal[27]), .in_7(control_signal[26]), .in_14(control_signal[25]),
    .in_6(control_signal[24]), .Branch(Branch_flush), .jump(Jump_flush), ._6_bits_IMM(_6_bits_immediate));
  not not_1 (not_1_out, stall);
  Register #(.width(12)) u_PC_2 (.D(NEXT_PC), .en(not_1_out), .Q(PC), .clk(CLK), .clr(clear));
  Clock clock_1 (.out(CLK));
  or or_1 (or_1_out, Branch_flush, Jump_flush);
  Adder #(.width(12)) adder_1 (.a(PC_if_id), .b(12'h2), .out(adder_1_out));  // open: cin, cout
  ROM #(.addrWidth(12), .dataWidth(16)) rom_1 (.addr(PC), .data(rom_1_data));  // open: sel
  assign PC_EXT = {{4{1'b0}}, adder_1_out};  // Bit_Extender bit_extender_1
  instruction_memory instruction_memory_1 (
    .iNSTRUCTION(Ins), ._12_bit_immediate(_12_bits_immediate), ._6_bit_immediate(_6_bits_immediate),
    ._4_bit_OpCode(_4_bits_opcode), ._3_bit_Rs(_3_bits_Rs), ._3_bit_Rt(_3_bits_Rt), ._3_bit_Rd(_3_bits_Rd),
    ._3_bit_R_Func(_3_bits_fn), ._4_bits_ALU_con(_4_bits_ALU_CON));
  Multiplexer #(.width(16), .enable("false")) multiplexer_1 (
    .in0(rom_1_data), .in1({16{1'b0}}), .out(multiplexer_1_out), .sel(or_1_out));
  IF_ID if_id_1 (.PC(PC), .Ins(multiplexer_1_out), .PC_2(PC_if_id), .CLK_2(CLK), .Ins_2(Ins), .CLK(not_2_out));
  not not_2 (not_2_out, stall);
  Multiplexer #(.width(3)) multiplexer_2 (
    .in0(_3_bits_Rt), .in1(_3_bits_Rd), .out(RD), .sel(control_signal[6]));  // open: en
  Multiplexer #(.width(16), .enable("false")) multiplexer_3 (
    .in0(out_12), .in1(PC_EXT), .out(multiplexer_3_out), .sel(or_2_out));
  or or_2 (or_2_out, control_signal[24], control_signal[26]);
  Multiplexer #(.width(3), .enable("false")) multiplexer_4 (
    .in0(out_10), .in1(3'b111), .out(multiplexer_4_out), .sel(control_signal[26]));
  Multiplexer #(.width(3), .enable("false")) multiplexer_5 (
    .in0(_3_bits_Rs), .in1(3'b111), .out(Ra), .sel(control_signal[25]));
  control_unit control_unit_1 (
    .fn(_3_bits_fn), .ALU_SRC(ALU_SRC), .Branch_Zero(B_Z), .MEM_Read(control_signal[2]),
    .MEM_Write(control_signal[3]), .MEM_To_Register(control_signal[4]), .REG_Write(control_signal[5]),
    .REG_DST(control_signal[6]), .J(control_signal[27]), .JAL(control_signal[26]), .JR(control_signal[25]),
    .JALR(control_signal[24]), .BEQ(BEQ), .BNE(BNE), .BLT(BLT), .BGT(BGT), .BLTZ(BLTZ), .BLTEZ(BLEZ),
    .BGTZ(BGTZ), .BGTEZ(BGEZ), .OpCode(_4_bits_opcode), .LUI(LUI), .ALU_OP(ALU_OP), .in_3(_3_bits_Rt),
    .out_6(R), .out_11(I));
  Multiplexer #(.width(3), .enable("false")) multiplexer_6 (
    .in0(multiplexer_4_out), .in1(3'b001), .out(multiplexer_6_out), .sel(LUI));
  Multiplexer #(.width(3), .enable("false")) multiplexer_7 (
    .in0(_3_bits_Rt), .in1(3'b000), .out(multiplexer_7_out), .sel(or_3_out));
  or or_3 (or_3_out, control_signal[24], B_Z, control_signal[25]);
  Multiplexer #(.width(16), .enable("false")) multiplexer_8 (
    .in0(multiplexer_3_out), .in1(_12_bits_EXT), .out(out_14), .sel(LUI));
  Multiplexer #(.width(3), .enable("false")) multiplexer_9 (
    .in0(multiplexer_6_out), .in1(3'b000), .out(multiplexer_9_out), .sel(control_signal[25]));
  Multiplexer #(.enable("false")) multiplexer_10 (
    .in0(control_signal_3[5]), .in1(control_signal[5]), .out(multiplexer_10_out), .sel(or_4_out));
  or or_4 (or_4_out, control_signal[26], LUI);
  Regster_File_main main_1 (
    .Write_Register(multiplexer_9_out), .Read_Register1(Ra), .in_3(multiplexer_7_out), .in_4(out_14),
    .out_7(data1), .out_8(data2), .in_5(multiplexer_10_out), .clock(CLK), .out_9(out_2), .out_10(out_3),
    .out_11(out_4), .out_12(out_5), .out_13(out_6), .out_14(out_7), .out_15(out_8), .out_16(out_9));
  or or_5 (or_5_out, Branch_flush, stall);
  Comparator #(.width(16), .mode("unsigned")) comparator_1 (.a(Bus_A), .b(Bus_B), .gt(L), .eq(EQ), .lt(G));
  Multiplexer #(.width(28), .enable("false")) multiplexer_11 (
    .in0({control_signal[27:24], BGEZ, BLEZ, BGTZ, BGT, BLTZ, BLT, BNE, BEQ, ALU_SRC, _4_bits_opcode, _4_bits_ALU_CON, control_signal[6:2], ALU_OP}),
    .in1({28{1'b0}}), .out(multiplexer_11_out), .sel(or_5_out));
  Multiplexer #(.width(16), .enable("false")) multiplexer_12 (
    .in0(data2), .in1(ALU_out), .out(multiplexer_12_out), .sel(Forword_sw));
  ALU_CONTROL alu_control_1 (
    .ALU_SELECT(ALU_OPERATION), .INPUT(out_11[10:7]), .sel(out_11[1:0]), .opcode(out_11[14:11]),
    .logic_sel(_2_bits_ALU_SEL));
  Multiplexer #(.width(16), .enable("false")) multiplexer_13 (
    .in0(data2), .in1(_6_bits_EXT), .out(multiplexer_13_out), .sel(ALU_SRC));
  Multiplexer #(.select(2), .width(16), .enable("false")) multiplexer_14 (
    .in0(data1), .in1(ALU_out), .in2(Mem), .in3(out_12), .out(Bus_A), .sel(Forword_A));
  ID_EX id_ex_1 (
    .Imm6(_6_bits_immediate), .BusA(Bus_A), .BusB(Bus_B), .Rd_2(_3_bits_Rd), .Rs(_3_bits_Rs),
    .Rt(_3_bits_Rt), .Func(_3_bits_fn), .Imm12(_12_bits_immediate), .opcode(_4_bits_opcode),
    .Imm6_2(_6_bits_immediate_1), .BusA_2(Bus_A_1), .BusB_3(Bus_B_1), .Rd_4(_3_bits_Rd_1),
    .Rs_2(_3_bits_Rs_1), .Rt_2(_3_bits_Rt_1), .Func_2(_3_bits_fn_1), .Imm12_2(_12_bits_immediate_1),
    .opcode_2(_4_bits_opcode_1_t), .CLK(CLK), .pc_next(PC_if_id), .control_signal(multiplexer_11_out),
    .control_signal_2(out_11), .pc_next_2(PC_1), .RD(RD), .RD_3(RD1), .BusB_2(multiplexer_12_out),
    .BusB_4(data_1));
  Multiplexer #(.select(2), .width(16), .enable("false")) multiplexer_15 (
    .in0(multiplexer_13_out), .in1(ALU_out), .in2(Mem), .in3(out_12), .out(Bus_B), .sel(Forword_B));
  forword_unit_main main_2 (
    .Rd_WB(out_10), .ForwarA(Forword_A), .Forward_B(Forword_B), .RegWrt_Mem_WB(control_signal_2[5]),
    .RegWrt_WB(control_signal_3[5]), .RegWrt_Ex_Mem(out_11[5]), .Ra(Ra), .Rb(_3_bits_Rt), .Mem_WB_Rd(RD2),
    .Ex_Mem_Rd(RD1), .IF_ID_Mem(control_signal[2]), .stall(stall), .ID_EX_Mem(out_11[2]),
    .MemWrite(control_signal[3]), .out_14(Forword_sw));
  assign bit_extender_2_out = {{4{_12_bits_immediate[11]}}, _12_bits_immediate};  // Bit_Extender bit_extender_2
  Shifter #(.width(16)) shifter_1 (.in(bit_extender_2_out), .\dist (4'b0100), .out(_12_bits_EXT));
  assign _6_bits_EXT = {{10{_6_bits_immediate[5]}}, _6_bits_immediate};  // Bit_Extender bit_extender_3
  ALU alu_1 (
    .A(Bus_A_1), .B(Bus_B_1), .ALU_RESULT(ALU_out), .ZERO_FLAG(Zero_Flag), .GREAT_FLAG(Great_Flag),
    .LESS_FLAG(Less_Flag), .ALU_OPERATION(ALU_OPERATION), .sel(_2_bits_ALU_SEL));  // open: OVER_FLOW_A, OVER_FLOW_S
  EX_MEM ex_mem_1 (
    .pc_next(PC_1), .pc_next_2(PC_2), .control_signal(out_11),
    .control_signal_2({control_signal_2[27:24], BGEZ2, BLEZ2, BGTZ2, BGT2, BLTZ2, BLT2, BNE2, BEQ2, ALU_SRC_2, control_signal_2[14:2], ALU_OP_2}),
    .ALU_out(ALU_out), .ALU_out_2({ALU_Result, out_13}), .BusA(Bus_A_1), .BusA_2(Bus_A_2), .BusB(data_1),
    .BusB_2(Bus_B_2), .Rd(_3_bits_Rd_1), .Rd_3(_3_bits_Rd_2), .Rs(_3_bits_Rs_1), .Rs_2(_3_bits_Rs_2),
    .Rt(_3_bits_Rt_1), .Rt_2(_3_bits_Rt_2), .CLK(CLK), .RD_2(RD1), .Rd_4(RD2));
  RAM #(.addrWidth(12), .dataWidth(16), .bus("separate")) ram_1 (
    .addr(out_13), .din(Bus_B_2), .data(Mem), .str(control_signal_2[3]), .clk(CLK), .ld(control_signal_2[2]));  // open: sel, clr
  MEM_WB mem_wb_1 (
    .control_signal({control_signal_2[27:24], BGEZ2, BLEZ2, BGTZ2, BGT2, BLTZ2, BLT2, BNE2, BEQ2, ALU_SRC_2, control_signal_2[14:2], ALU_OP_2}),
    .ALU_out({ALU_Result, out_13}), .MEM_out(Mem), .Rd(_3_bits_Rd_2),
    .control_signal_2({control_signal_3[27:24], BGEZ3, BLEZ3, BGTZ3, BGT3, BLTZ3, BLT3, BNE3, BEQ3, ALU_SRC_3, control_signal_3[14:2], ALU_OP_3}),
    .ALU_out_2(mem_wb_1_alu_out_2), .MEM_out_2(mem_wb_1_mem_out_2), .Rd_3(_3_bits_Rd_3), .CLK(CLK),
    .RD_2(RD2), .Rd_4(out_10));
  Multiplexer #(.width(16), .enable("false")) multiplexer_16 (
    .in0(mem_wb_1_alu_out_2), .in1(mem_wb_1_mem_out_2), .out(out_12), .sel(control_signal_3[4]));
  // also tied to GND on the sheet: control_signal_3[27]

  // Other names for the same wires on the sheet: Adress[11:0] = out_13; ALU_Result[11:0] = out_13;
  //   control_signal (some bits) = {BGEZ, BLEZ, BGTZ, BGT, BLTZ, BLT, BNE, BEQ, ALU_SRC, _4_bits_opcode, _4_bits_ALU_CON, ALU_OP};
  //   MEM_READ = control_signal[2]; MEM_WR = control_signal[3]; MEM_TO_REG = control_signal[4];
  //   REG_WR = control_signal[5]; REG_DST = control_signal[6]; JALR = control_signal[24]; JR = control_signal[25];
  //   JAL = control_signal[26]; J = control_signal[27]; ALU_OP_1[1:0] = out_11[1:0]; control_signal_1[27:0] = out_11;
  //   MEM_READ_1 = out_11[2]; MEM_WR_1 = out_11[3]; MEM_TO_REG_1 = out_11[4]; REG_WR_1 = out_11[5];
  //   REG_DST_1 = out_11[6]; _4_bits_ALU_CON_1[3:0] = out_11[10:7]; _4_bits_opcode_1[3:0] = out_11[14:11];
  //   ALU_SRC_1 = out_11[15]; BEQ1 = out_11[16]; BNE1 = out_11[17]; BLT1 = out_11[18]; BLTZ1 = out_11[19];
  //   BGT1 = out_11[20]; BGTZ1 = out_11[21]; BLEZ1 = out_11[22]; BGEZ1 = out_11[23]; JALR1 = out_11[24];
  //   JR1 = out_11[25]; JAL1 = out_11[26]; J1 = out_11[27];
  //   control_signal_2 (some bits) = {BGEZ2, BLEZ2, BGTZ2, BGT2, BLTZ2, BLT2, BNE2, BEQ2, ALU_SRC_2, ALU_OP_2};
  //   MEM_READ_2 = control_signal_2[2]; MEM_WR_2 = control_signal_2[3]; MEM_TO_REG_2 = control_signal_2[4];
  //   REG_WR_2 = control_signal_2[5]; REG_DST_2 = control_signal_2[6]; R111[3:0] = control_signal_2[10:7];
  //   R11[3:0] = control_signal_2[14:11]; JALR2 = control_signal_2[24]; JR2 = control_signal_2[25];
  //   JAL2 = control_signal_2[26]; J2 = control_signal_2[27];
  //   control_signal_3 (some bits) = {BGEZ3, BLEZ3, BGTZ3, BGT3, BLTZ3, BLT3, BNE3, BEQ3, ALU_SRC_3, ALU_OP_3};
  //   MEM_READ_3 = control_signal_3[2]; MEM_WR_3 = control_signal_3[3]; MEM_TO_REG_3 = control_signal_3[4];
  //   REG_WR_3 = control_signal_3[5]; REG_DST_3 = control_signal_3[6]; R22[3:0] = control_signal_3[10:7];
  //   R222[3:0] = control_signal_3[14:11]; JALR3 = control_signal_3[24]; JR3 = control_signal_3[25];
  //   JAL3 = control_signal_3[26]; R0[15:0] = out_2; R1[15:0] = out_3; R2[15:0] = out_4; R3[15:0] = out_5;
  //   R4[15:0] = out_6; R5[15:0] = out_7; R6[15:0] = out_8; R7[15:0] = out_9; Rb[2:0] = _3_bits_Rt; RD3[2:0] = out_10;
  //   Write_Data[15:0] = out_12

  // Notes on the sheet:
  //   contents of rom_1 (hex, n*v repeats v):
  //   a384 0 8354 0 35b 0 2040 0 2081 0 20c2 0 890a 0 1921 0 1520 0 14f2 0 4c02 0 1290 0 403b 0 3100 0
  //   b012 0 55c 0 1b68 0 403f 0 4e9 0 2040 0 2285 0 22c6 0 4e0 0 3100 0 1e06
endmodule

module IF_ID (
  input  [11:0] PC,
  input  [15:0] Ins,
  input  CLK,
  input  CLK_2,
  output [11:0] PC_2,
  output [15:0] Ins_2
);

  Register #(.width(12)) register_1 (.D(PC), .en(CLK), .Q(PC_2), .clk(CLK_2), .clr(1'b0));
  Register #(.width(16)) register_2 (.D(Ins), .en(CLK), .Q(Ins_2), .clk(CLK_2), .clr(1'b0));
endmodule

module ID_EX (
  input  [11:0] pc_next,
  input  [27:0] control_signal,
  input  [5:0] Imm6,
  input  [2:0] RD,
  input  [15:0] BusA,
  input  [15:0] BusB,
  input  [2:0] Rd_2,
  input  [2:0] Rs,
  input  [2:0] Rt,
  input  [2:0] Func,
  input  [11:0] Imm12,
  input  [3:0] opcode,
  input  [15:0] BusB_2,
  input  CLK,
  output [11:0] pc_next_2,
  output [27:0] control_signal_2,
  output [5:0] Imm6_2,
  output [2:0] RD_3,
  output [15:0] BusA_2,
  output [15:0] BusB_3,
  output [2:0] Rd_4,
  output [2:0] Rs_2,
  output [2:0] Rt_2,
  output [2:0] Func_2,
  output [11:0] Imm12_2,
  output [3:0] opcode_2,
  output [15:0] BusB_4
);

  Register #(.width(12)) register_1 (.D(pc_next), .en(1'b1), .Q(pc_next_2), .clk(CLK), .clr(1'b0));
  Register #(.width(28)) register_2 (.D(control_signal), .en(1'b1), .Q(control_signal_2), .clk(CLK), .clr(1'b0));
  Register #(.width(6)) register_3 (.D(Imm6), .en(1'b1), .Q(Imm6_2), .clk(CLK), .clr(1'b0));
  Register #(.width(3)) register_4 (.D(RD), .en(1'b1), .Q(RD_3), .clk(CLK), .clr(1'b0));
  Register #(.width(16)) register_5 (.D(BusA), .en(1'b1), .Q(BusA_2), .clk(CLK), .clr(1'b0));
  Register #(.width(16)) register_6 (.D(BusB), .en(1'b1), .Q(BusB_3), .clk(CLK), .clr(1'b0));
  Register #(.width(3)) register_7 (.D(Rd_2), .en(1'b1), .Q(Rd_4), .clk(CLK), .clr(1'b0));
  Register #(.width(3)) register_8 (.D(Rs), .en(1'b1), .Q(Rs_2), .clk(CLK), .clr(1'b0));
  Register #(.width(3)) register_9 (.D(Rt), .en(1'b1), .Q(Rt_2), .clk(CLK), .clr(1'b0));
  Register #(.width(3)) register_10 (.D(Func), .en(1'b1), .Q(Func_2), .clk(CLK), .clr(1'b0));
  Register #(.width(12)) register_11 (.D(Imm12), .en(1'b1), .Q(Imm12_2), .clk(CLK), .clr(1'b0));
  Register #(.width(4)) register_12 (.D(opcode), .en(1'b1), .Q(opcode_2), .clk(CLK), .clr(1'b0));
  Register #(.width(16)) register_13 (.D(BusB_2), .en(1'b1), .Q(BusB_4), .clk(CLK), .clr(1'b0));
endmodule

module Hazardl (
  input  branch,
  input  ID_EX_Jump,
  input  ID_EX_MemRead,
  input  [2:0] IF_ID_Rt,
  input  [2:0] ID_EX_Rd,
  input  [2:0] IF_ID_Rs,
  output branch_flush,
  output JumpStall,
  output JumpFlush,
  output LoadStall
);

  wire comparator_1_eq, comparator_2_eq, or_1_out;

  buf buffer_1 (branch_flush, branch);
  Comparator #(.width(3)) comparator_1 (.a(IF_ID_Rt), .b(ID_EX_Rd), .eq(comparator_1_eq));  // open: gt, lt
  Comparator #(.width(3)) comparator_2 (.a(ID_EX_Rd), .b(IF_ID_Rs), .eq(comparator_2_eq));  // open: gt, lt
  buf buffer_2 (JumpFlush, ID_EX_Jump);
  or or_1 (or_1_out, comparator_1_eq, comparator_2_eq);
  and and_1 (LoadStall, ID_EX_MemRead, or_1_out);

  assign JumpStall = JumpFlush;
endmodule

module EX_MEM (
  input  [11:0] pc_next,
  input  [27:0] control_signal,
  input  [15:0] ALU_out,
  input  [15:0] BusA,
  input  [15:0] BusB,
  input  [2:0] Rd,
  input  [2:0] Rs,
  input  [2:0] Rt,
  input  [2:0] RD_2,
  input  CLK,
  output [11:0] pc_next_2,
  output [27:0] control_signal_2,
  output [15:0] ALU_out_2,
  output [15:0] BusA_2,
  output [15:0] BusB_2,
  output [2:0] Rd_3,
  output [2:0] Rs_2,
  output [2:0] Rt_2,
  output [2:0] Rd_4
);

  Register #(.width(12)) register_1 (.D(pc_next), .en(1'b1), .Q(pc_next_2), .clk(CLK), .clr(1'b0));
  Register #(.width(28)) register_2 (.D(control_signal), .en(1'b1), .Q(control_signal_2), .clk(CLK), .clr(1'b0));
  Register #(.width(16)) register_3 (.D(ALU_out), .en(1'b1), .Q(ALU_out_2), .clk(CLK), .clr(1'b0));
  Register #(.width(16)) register_4 (.D(BusA), .en(1'b1), .Q(BusA_2), .clk(CLK), .clr(1'b0));
  Register #(.width(16)) register_5 (.D(BusB), .en(1'b1), .Q(BusB_2), .clk(CLK), .clr(1'b0));
  Register #(.width(3)) register_6 (.D(Rd), .en(1'b1), .Q(Rd_3), .clk(CLK), .clr(1'b0));
  Register #(.width(3)) register_7 (.D(Rs), .en(1'b1), .Q(Rs_2), .clk(CLK), .clr(1'b0));
  Register #(.width(3)) register_8 (.D(Rt), .en(1'b1), .Q(Rt_2), .clk(CLK), .clr(1'b0));
  Register #(.width(3)) register_9 (.D(RD_2), .en(1'b1), .Q(Rd_4), .clk(CLK), .clr(1'b0));
endmodule

module MEM_WB (
  input  [27:0] control_signal,
  input  [15:0] ALU_out,
  input  [15:0] MEM_out,
  input  [2:0] Rd,
  input  [2:0] RD_2,
  input  CLK,
  output [27:0] control_signal_2,
  output [15:0] ALU_out_2,
  output [15:0] MEM_out_2,
  output [2:0] Rd_3,
  output [2:0] Rd_4
);

  Register #(.width(28)) register_1 (.D(control_signal), .en(1'b1), .Q(control_signal_2), .clk(CLK), .clr(1'b0));
  Register #(.width(16)) register_2 (.D(ALU_out), .en(1'b1), .Q(ALU_out_2), .clk(CLK), .clr(1'b0));
  Register #(.width(16)) register_3 (.D(MEM_out), .en(1'b1), .Q(MEM_out_2), .clk(CLK), .clr(1'b0));
  Register #(.width(3)) register_4 (.D(Rd), .en(1'b1), .Q(Rd_3), .clk(CLK), .clr(1'b0));
  Register #(.width(3)) register_5 (.D(RD_2), .en(1'b1), .Q(Rd_4), .clk(CLK), .clr(1'b0));
endmodule

module Forword_control (
  input  [2:0] Mem_WB_Rd,
  input  RegWrt_Mem_WB,
  input  RegWrt_Ex_Mem,
  input  [2:0] Ra,
  input  [2:0] Rb,
  input  [2:0] Ex_Mem_Rd,
  output [1:0] Forward_A,
  output [1:0] Forward_B
);

  wire comparator_1_eq, comparator_2_eq, comparator_3_eq, comparator_4_eq, or_1_out, or_2_out;

  Comparator #(.width(3)) comparator_1 (.a(Ex_Mem_Rd), .b(Ra), .eq(comparator_1_eq));  // open: gt, lt
  Comparator #(.width(3)) comparator_2 (.a(Ex_Mem_Rd), .b(Rb), .eq(comparator_2_eq));  // open: gt, lt
  Comparator #(.width(3)) comparator_3 (.a(Mem_WB_Rd), .b(Ra), .eq(comparator_3_eq));  // open: gt, lt
  Comparator #(.width(3)) comparator_4 (.a(Mem_WB_Rd), .b(Rb), .eq(comparator_4_eq));  // open: gt, lt
  or or_1 (or_1_out, Ex_Mem_Rd[0], Ex_Mem_Rd[1], Ex_Mem_Rd[2]);
  or or_2 (or_2_out, Mem_WB_Rd[0], Mem_WB_Rd[1], Mem_WB_Rd[2]);
  and and_1 (Forward_A[0], RegWrt_Ex_Mem, or_1_out, comparator_1_eq);
  and and_2 (Forward_B[0], RegWrt_Ex_Mem, or_1_out, comparator_2_eq);
  and and_3 (Forward_A[1], RegWrt_Mem_WB, comparator_3_eq, or_2_out);
  and and_4 (Forward_B[1], RegWrt_Mem_WB, comparator_4_eq, or_2_out);
endmodule
