// Logisim project PC.circ as structural Verilog: 1 circuit, main circuit PC
module PC (
  input  [11:0] PC,
  input  [5:0] _6_bits_IMM,
  input  [11:0] _12_bits_IMM,
  input  [15:0] RD_1,
  input  in_5,
  input  in_6,
  input  in_7,
  input  in_8,
  input  in_9,
  input  in_10,
  input  in_11,
  input  in_12,
  input  in_13,
  input  in_14,
  input  in_15,
  input  in_16,
  input  in_17,
  input  in_18,
  input  in_19,
  output [11:0] RESULT,
  output Branch,
  output jump
);

  wire and_1_out, and_2_out, and_3_out, and_4_out, and_5_out, and_6_out, and_7_out, and_8_out, not_1_out,
       or_2_out, or_3_out, or_4_out, or_5_out;
  wire [5:0] adder_1_out;
  wire [11:0] _12_bits_IMM_B, _12_bits_IMM_J, bit_extender_1_out, multiplexer_1_out, multiplexer_2_out, PC_2,
       shifter_2_out;

  Adder #(.width(6)) adder_1 (.a(_6_bits_IMM), .b({6{1'b1}}), .out(adder_1_out));  // open: cin, cout
  assign bit_extender_1_out = {{6{adder_1_out[5]}}, adder_1_out};  // Bit_Extender bit_extender_1
  Shifter #(.width(12)) shifter_1 (.in(_12_bits_IMM), .\dist (4'b0001), .out(_12_bits_IMM_J));
  Shifter #(.width(12)) shifter_2 (.in(bit_extender_1_out), .\dist (4'b0001), .out(shifter_2_out));
  Adder #(.width(12)) adder_2 (.a(PC_2), .b(shifter_2_out), .out(_12_bits_IMM_B));  // open: cin, cout
  Adder #(.width(12)) adder_3 (.a(PC), .b(12'h2), .out(PC_2));  // open: cin, cout
  and and_1 (and_1_out, in_13, in_18);
  and and_2 (and_2_out, in_5, in_9);
  and and_3 (and_3_out, in_12, in_19);
  and and_4 (and_4_out, not_1_out, in_11);
  not not_1 (not_1_out, in_12);
  Multiplexer #(.width(12)) multiplexer_1 (
    .in0(PC_2), .in1(_12_bits_IMM_B), .out(multiplexer_1_out), .sel(Branch));  // open: en
  or or_1 (Branch, and_1_out, and_2_out, and_3_out, and_4_out, and_5_out, and_6_out, and_7_out, and_8_out);
  and and_5 (and_5_out, in_13, in_16);
  or or_2 (or_2_out, in_13, in_12);
  and and_6 (and_6_out, or_2_out, in_10);
  and and_7 (and_7_out, in_5, in_17);
  or or_3 (or_3_out, in_5, in_12);
  and and_8 (and_8_out, or_3_out, in_8);
  Multiplexer #(.width(12)) multiplexer_2 (
    .in0(multiplexer_1_out), .in1(_12_bits_IMM_J), .out(multiplexer_2_out), .sel(or_4_out));  // open: en
  or or_4 (or_4_out, in_15, in_7);
  or or_5 (or_5_out, in_14, in_6);
  Multiplexer #(.width(12)) multiplexer_3 (
    .in0(multiplexer_2_out), .in1(RD_1[11:0]), .out(RESULT), .sel(or_5_out));  // open: en
  or or_6 (jump, or_4_out, or_5_out);

  // Other names for the same wires on the sheet: BEQ = in_19; BGEZ = in_8; BGT = in_9; BGTZ = in_17; BLEZ = in_10;
  //   BLT = in_18; BLTZ = in_16; BNE = in_11; GREAT = in_5; J = in_15; JAL = in_7; JALR = in_6; JR = in_14;
  //   LESS = in_13; _12_bits_RD_1[11:0] = RD_1[11:0]; ZERO = in_12

  // Notes on the sheet:
  //   ,BLT
  //   BGT
  //   BEQ
  //   BNE
  //   BLTZ
  //   BLEZ
  //   BGTZ
  //   BGEZ
endmodule
