// Logisim project Regster File.circ as structural Verilog: 1 circuit, main circuit main
module main (
  input  [2:0] Write_Register,
  input  [2:0] Read_Register1,
  input  [2:0] in_3,
  input  [15:0] in_4,
  input  in_5,
  input  clock,
  output [15:0] out_7,
  output [15:0] out_8,
  output [15:0] out_9,
  output [15:0] out_10,
  output [15:0] out_11,
  output [15:0] out_12,
  output [15:0] out_13,
  output [15:0] out_14,
  output [15:0] out_15,
  output [15:0] out_16
);

  wire and_1_out, and_2_out, and_3_out, and_4_out, and_5_out, and_6_out, and_7_out, decoder_1_out1,
       decoder_1_out2, decoder_1_out3, decoder_1_out4, decoder_1_out5, decoder_1_out6, decoder_1_out7,
       undriven;

  Decoder #(.select(3)) decoder_1 (
    .out1(decoder_1_out1), .out2(decoder_1_out2), .out3(decoder_1_out3), .out4(decoder_1_out4),
    .out5(decoder_1_out5), .out6(decoder_1_out6), .out7(decoder_1_out7), .sel(Write_Register));  // open: out0, en
  and and_1 (and_1_out, decoder_1_out1, in_5);
  and and_2 (and_2_out, decoder_1_out2, in_5);
  and and_3 (and_3_out, decoder_1_out3, in_5);
  and and_4 (and_4_out, decoder_1_out4, in_5);
  and and_5 (and_5_out, decoder_1_out5, in_5);
  and and_6 (and_6_out, decoder_1_out6, in_5);
  and and_7 (and_7_out, decoder_1_out7, in_5);
  Register #(.width(16)) register_1 (.D({16{1'b0}}), .Q(out_9), .clk(clock), .clr(undriven));  // open: en
  Register #(.width(16)) register_2 (.D(in_4), .en(and_1_out), .Q(out_10), .clk(clock), .clr(undriven));
  Register #(.width(16)) register_3 (.D(in_4), .en(and_2_out), .Q(out_11), .clk(clock), .clr(undriven));
  Register #(.width(16)) register_4 (.D(in_4), .en(and_3_out), .Q(out_12), .clk(clock), .clr(undriven));
  Register #(.width(16)) register_5 (.D(in_4), .en(and_4_out), .Q(out_13), .clk(clock), .clr(undriven));
  Register #(.width(16)) register_6 (.D(in_4), .en(and_5_out), .Q(out_14), .clk(clock), .clr(undriven));
  Register #(.width(16)) register_7 (.D(in_4), .en(and_6_out), .Q(out_15), .clk(clock), .clr(undriven));
  Register #(.width(16)) register_8 (.D(in_4), .en(and_7_out), .Q(out_16), .clk(clock), .clr(undriven));
  Multiplexer #(.select(3), .width(16)) multiplexer_1 (
    .in0(out_9), .in1(out_10), .in2(out_11), .in3(out_12), .in4(out_13), .in5(out_14), .in6(out_15),
    .in7(out_16), .out(out_7), .sel(Read_Register1));  // open: en
  Multiplexer #(.select(3), .width(16)) multiplexer_2 (
    .in0(out_9), .in1(out_10), .in2(out_11), .in3(out_12), .in4(out_13), .in5(out_14), .in6(out_15),
    .in7(out_16), .out(out_8), .sel(in_3));  // open: en

  // Other names for the same wires on the sheet: R0[15:0] = out_9; R1[15:0] = out_10; R2[15:0] = out_11;
  //   R3[15:0] = out_12; R4[15:0] = out_13; R5[15:0] = out_14; R6[15:0] = out_15; R7[15:0] = out_16

  // Notes on the sheet:
  //   Read Register2
  //   Write Data
  //   RegWrite
  //   Read Data 1
  //   Read Data 2
endmodule
