// Logisim project forword unit.circ as structural Verilog: 2 circuits, main circuit main
module main (
  input  [2:0] Mem_WB_Rd,
  input  [2:0] Rd_WB,
  input  RegWrt_Mem_WB,
  input  RegWrt_Ex_Mem,
  input  [2:0] Ra,
  input  [2:0] Rb,
  input  [2:0] Ex_Mem_Rd,
  input  RegWrt_WB,
  input  ID_EX_Mem,
  input  MemWrite,
  input  IF_ID_Mem,
  output [1:0] ForwarA,
  output stall,
  output out_14,
  output [1:0] Forward_B
);

  wire and_1_out, and_2_out, and_3_out, and_4_out, and_5_out, and_6_out, and_8_out, and_9_out, and_10_out,
       and_11_out, comparator_1_eq, comparator_2_eq, comparator_3_eq, comparator_4_eq, comparator_5_eq,
       comparator_6_eq, not_1_out, not_2_out, not_3_out, not_4_out, or_1_out, or_2_out, or_3_out, or_8_out,
       or_9_out, p_revious_1_x, p_revious_1_y, p_revious_1_z, p_revious_2_x, p_revious_2_y, p_revious_2_z;

  not not_1 (not_1_out, IF_ID_Mem);
  Comparator #(.width(3)) comparator_1 (.a(Ex_Mem_Rd), .b(Ra), .eq(comparator_1_eq));  // open: gt, lt
  Comparator #(.width(3)) comparator_2 (.a(Ex_Mem_Rd), .b(Rb), .eq(comparator_2_eq));  // open: gt, lt
  Comparator #(.width(3)) comparator_3 (.a(Mem_WB_Rd), .b(Ra), .eq(comparator_3_eq));  // open: gt, lt
  Comparator #(.width(3)) comparator_4 (.a(Mem_WB_Rd), .b(Rb), .eq(comparator_4_eq));  // open: gt, lt
  or or_1 (or_1_out, Ex_Mem_Rd[0], Ex_Mem_Rd[1], Ex_Mem_Rd[2]);
  or or_2 (or_2_out, Mem_WB_Rd[0], Mem_WB_Rd[1], Mem_WB_Rd[2]);
  or or_3 (or_3_out, Rd_WB[0], Rd_WB[1], Rd_WB[2]);
  and and_1 (and_1_out, RegWrt_Ex_Mem, or_1_out, comparator_1_eq);
  and and_2 (and_2_out, RegWrt_Ex_Mem, or_1_out, comparator_2_eq);
  and and_3 (and_3_out, RegWrt_Mem_WB, comparator_3_eq, or_2_out);
  and and_4 (and_4_out, RegWrt_Mem_WB, comparator_4_eq, or_2_out);
  Comparator #(.width(3)) comparator_5 (.a(Rd_WB), .b(Ra), .eq(comparator_5_eq));  // open: gt, lt
  Comparator #(.width(3)) comparator_6 (.a(Rd_WB), .b(Rb), .eq(comparator_6_eq));  // open: gt, lt
  and and_5 (and_5_out, or_3_out, comparator_5_eq, RegWrt_WB);
  and and_6 (and_6_out, RegWrt_WB, comparator_6_eq, or_3_out);
  p_revious p_revious_1 (
    .a(and_1_out), .b(and_3_out), .c(and_5_out), .x(p_revious_1_x), .y(p_revious_1_y), .z(p_revious_1_z));
  and and_7 (out_14, and_2_out, MemWrite);
  not not_2 (not_2_out, MemWrite);
  and and_8 (and_8_out, not_2_out, and_2_out);
  p_revious p_revious_2 (
    .a(and_8_out), .b(and_4_out), .c(and_9_out), .x(p_revious_2_x), .y(p_revious_2_y), .z(p_revious_2_z));
  and and_9 (and_9_out, and_6_out, not_1_out);
  or or_4 (ForwarA[0], p_revious_1_x, p_revious_1_z);
  or or_5 (ForwarA[1], p_revious_1_y, p_revious_1_z);
  or or_6 (Forward_B[0], p_revious_2_x, p_revious_2_z);
  or or_7 (Forward_B[1], p_revious_2_y, p_revious_2_z);
  not not_3 (not_3_out, ForwarA[1]);
  and and_10 (and_10_out, ForwarA[0], not_3_out);
  and and_11 (and_11_out, Forward_B[0], not_4_out);
  not not_4 (not_4_out, Forward_B[1]);
  or or_8 (or_8_out, IF_ID_Mem, ID_EX_Mem);
  or or_9 (or_9_out, and_10_out, and_11_out);
  and and_12 (stall, or_8_out, or_9_out);
endmodule

module p_revious (
  input  a,
  input  b,
  input  c,
  output x,
  output y,
  output z
);

  wire not_1_out, not_2_out, not_3_out;

  not not_1 (not_1_out, a);
  not not_2 (not_2_out, a);
  not not_3 (not_3_out, b);
  and and_1 (y, not_1_out, b);
  and and_2 (z, not_2_out, not_3_out, c);

  assign x = a;
endmodule
