// Logisim project instruction memory.circ as structural Verilog: 1 circuit, main circuit instruction memory
module instruction_memory (
  input  [15:0] iNSTRUCTION,
  output [11:0] _12_bit_immediate,
  output [5:0] _6_bit_immediate,
  output [3:0] _4_bit_OpCode,
  output [2:0] _3_bit_Rs,
  output [2:0] _3_bit_Rt,
  output [2:0] _3_bit_Rd,
  output [2:0] _3_bit_R_Func,
  output [3:0] _4_bits_ALU_con
);


  assign _3_bit_R_Func = iNSTRUCTION[2:0];
  assign _3_bit_Rd = iNSTRUCTION[5:3];
  assign _3_bit_Rs = iNSTRUCTION[11:9];
  assign _3_bit_Rt = iNSTRUCTION[8:6];
  assign _4_bit_OpCode = iNSTRUCTION[15:12];
  assign _4_bits_ALU_con = {iNSTRUCTION[12], iNSTRUCTION[2:0]};
  assign _6_bit_immediate = iNSTRUCTION[5:0];
  assign _12_bit_immediate = iNSTRUCTION[11:0];

  // Other names for the same wires on the sheet: _13 = iNSTRUCTION[13]; _14 = iNSTRUCTION[14]; _15 = iNSTRUCTION[15];
  //   _12 = iNSTRUCTION[12]; _0 = iNSTRUCTION[0]; _1 = iNSTRUCTION[1]; _2 = iNSTRUCTION[2]; _3 = iNSTRUCTION[3];
  //   _4 = iNSTRUCTION[4]; _5 = iNSTRUCTION[5]; _6 = iNSTRUCTION[6]; _7 = iNSTRUCTION[7]; _8 = iNSTRUCTION[8];
  //   _9 = iNSTRUCTION[9]; _10 = iNSTRUCTION[10]; _11 = iNSTRUCTION[11]
endmodule
